// Logisim project 6502.circ as structural Verilog: 10 circuits, main circuit main
module main (
  input  [7:0] data_in,
  input  in_2,
  input  in_3,
  output [7:0] internal_data_bus,
  output [7:0] internal_abl,
  output [7:0] internal_abh
);

  wire alu_1_p2, clk_out, undriven, undriven_2, undriven_3, undriven_4, undriven_5, undriven_6, undriven_7,
       undriven_8, undriven_9, undriven_10, undriven_11, undriven_12, undriven_13, undriven_14, undriven_15;
  wire [7:0] ABH_output_byte, ABL_output_byte, alu_1_p1, buffer_8bit_1_data_out, DL_output_byte,
       mux_4_1_8bit_1_out_byte, mux_4_1_8bit_2_out_byte, mux_4_1_8bit_3_out_byte,
       process_state_register_output_byte, program_counter_1_p2, program_counter_1_p3, S_output_byte,
       undriven_16, X_output_byte, Y_output_byte;
  wire [15:0] wiring_split_2x8_to_16_1_word;

  Clock clk (.out(clk_out));
  wiring_split_2x8_to_16 wiring_split_2x8_to_16_1 (
    .low_byte(ABL_output_byte), .high_byte(ABH_output_byte), .word(wiring_split_2x8_to_16_1_word));
  RAM #(.addrWidth(16)) ram_1 (
    .addr(wiring_split_2x8_to_16_1_word), .we(undriven), .oe(in_2), .clk(clk_out), .din(internal_data_bus),
    .dout(internal_data_bus));
  // alu alu_1: pin names not known; wires that end beside it: alu_1_p1, alu_1_p2
  register_8bit ABL (
    .load_enable_acL(undriven_3), .Input_byte(internal_abl), .clk(clk_out), .output_byte(ABL_output_byte));
  register_8bit ABH (
    .load_enable_acL(undriven_2), .Input_byte(internal_abh), .clk(clk_out), .output_byte(ABH_output_byte));
  // register_8bit tmp: pin names not known; wires that end beside it: alu_1_p2
  register_8bit X (
    .load_enable_acL(undriven_8), .Input_byte(internal_data_bus), .clk(clk_out), .output_byte(X_output_byte));
  register_8bit Y (.load_enable_acL(undriven_7), .clk(clk_out), .output_byte(Y_output_byte));  // open: Input_byte
  register_8bit S (.load_enable_acL(undriven_6), .clk(clk_out), .output_byte(S_output_byte));  // open: Input_byte
  register_8bit A (.load_enable_acL(undriven_5), .clk(clk_out), .output_byte(alu_1_p1));  // open: Input_byte
  register_8bit DL (.load_enable_acL(in_3), .Input_byte(data_in), .clk(clk_out), .output_byte(DL_output_byte));
  register_8bit process_state_register (
    .load_enable_acL(undriven_4), .clk(clk_out), .output_byte(process_state_register_output_byte));  // open: Input_byte
  // program_counter program_counter_1: pin names not known; wires that end beside it: clk_out, program_counter_1_p2, program_counter_1_p3
  buffer_8bit buffer_8bit_1 (.data_in(undriven_16), .data_out(buffer_8bit_1_data_out));  // open: enable_acL
  mux_4_1_8bit mux_4_1_8bit_1 (
    .s1(undriven_9), .s0(undriven_10), .byte1(X_output_byte), .byte2(Y_output_byte), .byte3(S_output_byte),
    .byte4(alu_1_p1), .out_byte(mux_4_1_8bit_1_out_byte));
  mux_4_1_8bit mux_4_1_8bit_2 (
    .s1(undriven_9), .s0(undriven_10), .byte1(DL_output_byte), .byte2(process_state_register_output_byte),
    .out_byte(mux_4_1_8bit_2_out_byte));  // open: byte3, byte4
  mux_4_1_8bit mux_4_1_8bit_3 (
    .s1(undriven_12), .s0(undriven_11), .byte1(mux_4_1_8bit_1_out_byte), .byte2(mux_4_1_8bit_2_out_byte),
    .byte3(program_counter_1_p2), .byte4(program_counter_1_p3), .out_byte(mux_4_1_8bit_3_out_byte));
  // buffer_8bit buffer_8bit_2: pin names not known
  buffer_8bit data_bus_buffer (
    .enable_acL(undriven_15), .data_in(mux_4_1_8bit_3_out_byte), .data_out(internal_data_bus));
  buffer_8bit address_bus_low_buffer (
    .enable_acL(undriven_14), .data_in(mux_4_1_8bit_3_out_byte), .data_out(internal_abl));
  buffer_8bit address_bus_high_buffer (
    .enable_acL(undriven_13), .data_in(mux_4_1_8bit_3_out_byte), .data_out(internal_abh));
  // register_8bit instruction_register: pin names not known

  // Notes on the sheet:
  //   Controller section
  //   reg sel [s0,s1,s2,{pc_ce}]
  //   CONTROL PINS
  //   reg
endmodule

module program_counter (
  input  load_parallel_LB_acL,
  input  reset_acL,
  input  CountEnable,
  input  [7:0] LB_Input_acH,
  input  load_parallel_HB_acL,
  input  [7:0] H_Input_acH,
  input  clk,
  output [7:0] PC_OUT_LOW_BYTE,
  output [7:0] PC_OUT_HIGH_BYTE
);

  wire n7408_1_pin4, n7408_1_pin5, n74163_1_pin7, n74163_1_pin15, n74163_2_pin7;

  _74163 u_74163_1 (
    .pin1(reset_acL), .pin2(clk), .pin3(LB_Input_acH[4]), .pin4(LB_Input_acH[5]), .pin5(LB_Input_acH[6]),
    .pin6(LB_Input_acH[7]), .pin7(n74163_1_pin7), .pin15(n74163_1_pin15), .pin14(PC_OUT_LOW_BYTE[4]),
    .pin13(PC_OUT_LOW_BYTE[5]), .pin12(PC_OUT_LOW_BYTE[6]), .pin11(PC_OUT_LOW_BYTE[7]), .pin10(CountEnable),
    .pin9(load_parallel_LB_acL));
  _74163 u_74163_2 (
    .pin1(reset_acL), .pin2(clk), .pin3(H_Input_acH[4]), .pin4(H_Input_acH[5]), .pin5(H_Input_acH[6]),
    .pin6(H_Input_acH[7]), .pin7(n74163_2_pin7), .pin14(PC_OUT_HIGH_BYTE[4]), .pin13(PC_OUT_HIGH_BYTE[5]),
    .pin12(PC_OUT_HIGH_BYTE[6]), .pin11(PC_OUT_HIGH_BYTE[7]), .pin10(CountEnable), .pin9(load_parallel_HB_acL));  // open: pin15
  _74163 u_74163_3 (
    .pin1(reset_acL), .pin2(clk), .pin3(LB_Input_acH[0]), .pin4(LB_Input_acH[1]), .pin5(LB_Input_acH[2]),
    .pin6(LB_Input_acH[3]), .pin7(CountEnable), .pin15(n74163_1_pin7), .pin14(PC_OUT_LOW_BYTE[0]),
    .pin13(PC_OUT_LOW_BYTE[1]), .pin12(PC_OUT_LOW_BYTE[2]), .pin11(PC_OUT_LOW_BYTE[3]), .pin10(CountEnable),
    .pin9(load_parallel_LB_acL));
  _7408 u_7408_1 (
    .pin4(n7408_1_pin4), .pin5(n7408_1_pin5), .pin6(n74163_2_pin7), .pin13(n74163_1_pin7),
    .pin12(n74163_1_pin15), .pin11(n7408_1_pin5));  // open: pin1, pin2, pin3, pin10, pin9, pin8
  _74163 u_74163_4 (
    .pin1(reset_acL), .pin2(clk), .pin3(H_Input_acH[0]), .pin4(H_Input_acH[1]), .pin5(H_Input_acH[2]),
    .pin6(H_Input_acH[3]), .pin7(n7408_1_pin5), .pin15(n7408_1_pin4), .pin14(PC_OUT_HIGH_BYTE[0]),
    .pin13(PC_OUT_HIGH_BYTE[1]), .pin12(PC_OUT_HIGH_BYTE[2]), .pin11(PC_OUT_HIGH_BYTE[3]),
    .pin10(CountEnable), .pin9(load_parallel_HB_acL));

  // Notes on the sheet:
  //   LB
  //   UB
endmodule

module register_8bit (
  input  load_enable_acL,
  input  [7:0] Input_byte,
  input  clk,
  output [7:0] output_byte
);

  ttl_74194 ttl_74194_1 (
    .d1(Input_byte[1]), .d0(Input_byte[0]), .d2(Input_byte[2]), .d3(Input_byte[3]), .cp(clk),
    .in_6(load_enable_acL), .q0(output_byte[0]), .q1(output_byte[1]), .q2(output_byte[2]), .q3(output_byte[3]));
  ttl_74194 ttl_74194_2 (
    .d1(Input_byte[5]), .d0(Input_byte[4]), .d2(Input_byte[6]), .d3(Input_byte[7]), .cp(clk),
    .in_6(load_enable_acL), .q0(output_byte[4]), .q1(output_byte[5]), .q2(output_byte[6]), .q3(output_byte[7]));
endmodule

module ttl_74194 (
  input  d0,
  input  d1,
  input  d2,
  input  d3,
  input  cp,
  input  in_6,
  output q0,
  output q1,
  output q2,
  output q3
);

  wire not_1_out;

  not not_1 (not_1_out, in_6);
  Register #(.width(4)) register_1 (.D({d3, d2, d1, d0}), .en(not_1_out), .clk(cp), .Q({q3, q2, q1, q0}));  // open: clr
endmodule

module buffer_8bit (
  input  enable_acL,
  input  [7:0] data_in,
  output [7:0] data_out
);

  _74125 u_74125_1 (
    .pin1(enable_acL), .pin2(data_in[1]), .pin3(data_out[1]), .pin4(enable_acL), .pin5(data_in[0]),
    .pin6(data_out[0]), .pin13(enable_acL), .pin12(data_in[2]), .pin11(data_out[2]), .pin10(enable_acL),
    .pin9(data_in[3]), .pin8(data_out[3]));
  _74125 u_74125_2 (
    .pin1(enable_acL), .pin2(data_in[5]), .pin3(data_out[5]), .pin4(enable_acL), .pin5(data_in[4]),
    .pin6(data_out[4]), .pin13(enable_acL), .pin12(data_in[6]), .pin11(data_out[6]), .pin10(enable_acL),
    .pin9(data_in[7]), .pin8(data_out[7]));
endmodule

module alu (
  input  mux_s1,
  input  mux_s0,
  input  [7:0] address_low_byte,
  input  [7:0] address_high_byte,
  input  [7:0] accumulator_byte,
  input  s3,
  input  s2,
  input  s1,
  input  s0,
  input  carry_in_acL,
  input  [7:0] tmp_byte,
  input  mode,
  output zero_flag,
  output [7:0] out_14,
  output negative_flag
);

  wire n7402_1_pin1, n7402_1_pin4, n7402_1_pin10, n7402_1_pin13, n7408_1_pin4, n7408_1_pin5, n74181_1_p7;
  wire [7:0] mux_4_1_8bit_1_out_byte;

  // _74181 74181_1: pin names not known; wires that end beside it: tmp_byte[4], mux_4_1_8bit_1_out_byte[4], s3, s2, s1, s0, n74181_1_p7, mode, out_14[4], out_14[5], out_14[6], mux_4_1_8bit_1_out_byte[5], tmp_byte[5], mux_4_1_8bit_1_out_byte[6], tmp_byte[6], mux_4_1_8bit_1_out_byte[7], tmp_byte[7], negative_flag, carry_in_acL, mode, out_14[1], out_14[0], out_14[2], n74181_1_p7, out_14[3]
  mux_4_1_8bit mux_4_1_8bit_1 (
    .s1(mux_s1), .s0(mux_s0), .byte1(address_low_byte), .byte2(address_high_byte), .byte3(accumulator_byte),
    .out_byte(mux_4_1_8bit_1_out_byte));  // open: byte4
  // _74181 74181_2: pin names not known; wires that end beside it: tmp_byte[0], mux_4_1_8bit_1_out_byte[0], s3, s2, s1, s0, mux_4_1_8bit_1_out_byte[1], tmp_byte[1], mux_4_1_8bit_1_out_byte[2], tmp_byte[2], mux_4_1_8bit_1_out_byte[3], tmp_byte[3]
  _7402 u_7402_1 (
    .pin1(n7402_1_pin1), .pin2(out_14[1]), .pin3(out_14[0]), .pin4(n7402_1_pin4), .pin5(out_14[2]),
    .pin6(out_14[3]), .pin13(n7402_1_pin13), .pin12(out_14[6]), .pin11(negative_flag), .pin10(n7402_1_pin10),
    .pin9(out_14[5]), .pin8(out_14[4]));
  _7408 u_7408_1 (
    .pin4(n7408_1_pin4), .pin5(n7408_1_pin5), .pin6(zero_flag), .pin13(n7402_1_pin4), .pin12(n7402_1_pin1),
    .pin11(n7408_1_pin5), .pin10(n7402_1_pin13), .pin9(n7402_1_pin10), .pin8(n7408_1_pin4));  // open: pin1, pin2, pin3

  assign out_14[7] = negative_flag;

  // Notes on the sheet:
  //   flags
endmodule

module controller_sequencer (
);

  ROM #(.dataWidth(64)) rom_1 ();  // open: addr, data

  // Notes on the sheet:
  //   contents of rom_1 (hex, n*v repeats v):
  //   18 21 920 2000001200 18 21 920 10001200 18 21 920 80000001200 40020000000 920 2001200 10000000000
  //   102000000 10000000000 802000000 10000000000 84000000 10000000000 880000000 10000000000 404000000
  //   10000000000 500000000 10000000000 18 21 920 2001200 10000000000 18 21 920 80001200 10000000000 18 21
  //   920 400001200 10000000000 18 21 920 10001200 18 21 920 80000001200 40020000000 4000520 22a0
  //   10000000000 110000000 3004000 10000000000 810000000 3004000 10000000000 110000000 3040000
  //   10000000000 810000000 3040000 10000000000 0 18 21 920 10001200 3040000 10000000000 14000000 3800000
  //   10000000000 14000000 3010000 10000000000 10*0 110000000 81010000 10000000000 810000000 401010000
  //   10000000000 14000000 3020000 10000000000 110000000 81020000 10000000000 810000000 401020000
  //   10000000000 110000000 3080000 10000000000 810000000 3080000 10000000000 18 21 920 10001200 3080000
  //   10000000000 110000000 3008000 10000000000 810000000 3008000 10000000000 110000000 3100000
  //   10000000000 810000000 3100000 10000000000 18 21 920 10001200 3100000 10000000000 14000000 3200000
  //   10000000000 14000000 3400000 10000000000 18 21 920 10001200 18 21 920 80000001200 40020000000
  //   100000000004 10000000000 18 21 920 10001200 18 21 1000000000000 920 80000001200 40020000000
  //   100000000004 10000000000 18 21 920 10001200 18 21 200000000000 920 80000001200 40020000000
  //   100000000004 10000000000 18 21 920 10001200 18 21 400000000000 920 80000001200 40020000000
  //   100000000004 0 10000000000 20000000000 18 21 920 10001200 18 21 920 80000001200 40020000000
  //   4000000000008 1 100000000004 10000000000 2000000000004 10000000000 20000002000000 40000000000000
  //   10000000000 80000002000000 10000000000 0 0 100000004000000 10000000000 200000004000000 10000000000
  //   39*0 10000000000
endmodule

module mux_4_1_8bit (
  input  s1,
  input  s0,
  input  [7:0] byte1,
  input  [7:0] byte2,
  input  [7:0] byte3,
  input  [7:0] byte4,
  output [7:0] out_byte
);

  wire n74153_1_pin8, n74153_1_pin16;

  _74153 #(.VccGndPorts("true")) u_74153_1 (
    .pin2(s1), .pin3(byte4[0]), .pin4(byte3[0]), .pin5(byte2[0]), .pin6(byte1[0]), .pin7(out_byte[0]),
    .pin8(n74153_1_pin8), .pin16(n74153_1_pin16), .pin14(s0), .pin13(byte4[1]), .pin12(byte3[1]),
    .pin11(byte2[1]), .pin10(byte1[1]), .pin9(out_byte[1]));  // open: pin1, pin15
  _74153 #(.VccGndPorts("true")) u_74153_2 (
    .pin2(s1), .pin3(byte4[4]), .pin4(byte3[4]), .pin5(byte2[4]), .pin6(byte1[4]), .pin7(out_byte[4]),
    .pin8(n74153_1_pin8), .pin16(n74153_1_pin16), .pin14(s0), .pin13(byte4[5]), .pin12(byte3[5]),
    .pin11(byte2[5]), .pin10(byte1[5]), .pin9(out_byte[5]));  // open: pin1, pin15
  _74153 #(.VccGndPorts("true")) u_74153_3 (
    .pin2(s1), .pin3(byte4[2]), .pin4(byte3[2]), .pin5(byte2[2]), .pin6(byte1[2]), .pin7(out_byte[2]),
    .pin8(n74153_1_pin8), .pin16(n74153_1_pin16), .pin14(s0), .pin13(byte4[3]), .pin12(byte3[3]),
    .pin11(byte2[3]), .pin10(byte1[3]), .pin9(out_byte[3]));  // open: pin1, pin15
  _74153 #(.VccGndPorts("true")) u_74153_4 (
    .pin2(s1), .pin3(byte4[6]), .pin4(byte3[6]), .pin5(byte2[6]), .pin6(byte1[6]), .pin7(out_byte[6]),
    .pin8(n74153_1_pin8), .pin16(n74153_1_pin16), .pin14(s0), .pin13(byte4[7]), .pin12(byte3[7]),
    .pin11(byte2[7]), .pin10(byte1[7]), .pin9(out_byte[7]));  // open: pin1, pin15
  // also tied to GND on the sheet: n74153_1_pin8
  // also tied to VCC on the sheet: n74153_1_pin16
endmodule

module wiring_split_2x8_to_16 (
  input  [7:0] low_byte,
  input  [7:0] high_byte,
  output [15:0] word
);


  assign word = {high_byte, low_byte};
endmodule

module alu_74181 (
  input  S3,
  input  S2,
  input  S1,
  input  S0,
  input  B3,
  input  A3,
  input  B2,
  input  A2,
  input  B1,
  input  A1,
  input  B0,
  input  A0,
  input  M,
  input  Cn,
  output G,
  output Cn_4_24ca263e,
  output P,
  output F3,
  output F2,
  output A_B_3b64f046,
  output F1,
  output F0
);

  wire and_1_out, and_2_out, and_3_out, and_4_out, and_5_out, and_6_out, and_7_out, and_8_out, and_9_out,
       and_10_out, and_11_out, and_12_out, and_13_out, and_14_out, and_15_out, and_16_out, and_17_out,
       and_18_out, and_19_out, and_20_out, and_21_out, and_22_out, and_23_out, and_24_out, and_25_out,
       and_26_out, and_28_out, and_29_out, and_30_out, and_31_out, and_32_out, and_33_out, and_34_out,
       and_35_out, and_36_out, and_37_out, and_38_out, nand_2_out, nand_4_out, nor_2_out, nor_3_out,
       nor_4_out, nor_5_out, nor_6_out, nor_7_out, nor_8_out, nor_9_out, nor_10_out, nor_11_out, nor_12_out,
       not_1_out, not_2_out, not_3_out, not_4_out, not_5_out, not_6_out, not_7_out, not_8_out, not_9_out;

  and and_1 (and_1_out, nor_3_out, nor_3_out);
  nor nor_1 (G, and_1_out, and_3_out, and_2_out, and_5_out, and_5_out);
  and and_2 (and_2_out, nor_2_out, nor_4_out, nor_9_out);
  and and_3 (and_3_out, nor_2_out, nor_6_out);
  and and_4 (and_4_out, B3, S3, A3);
  nand nand_1 (Cn_4_24ca263e, G, nand_2_out);
  and and_5 (and_5_out, nor_2_out, nor_4_out, nor_7_out, nor_12_out, nor_12_out);
  nor nor_2 (nor_2_out, and_4_out, and_6_out);
  and and_6 (and_6_out, A3, S2, not_1_out);
  not not_1 (not_1_out, B3);
  nand nand_2 (nand_2_out, nor_2_out, nor_4_out, nor_7_out, nor_11_out, Cn);
  nand nand_3 (P, nor_2_out, nor_4_out, nor_7_out, nor_11_out, nor_11_out);
  nor nor_3 (nor_3_out, and_7_out, and_8_out, and_10_out);
  and and_7 (and_7_out, not_1_out, S1);
  and and_8 (and_8_out, S0, B3);
  and and_9 (and_9_out, nor_2_out, not_2_out);
  not not_2 (not_2_out, nor_3_out);
  and and_10 (and_10_out, A3, A3);
  and and_11 (and_11_out, nor_4_out, nor_7_out, nor_11_out, Cn, not_9_out);
  nor nor_4 (nor_4_out, and_12_out, and_13_out);
  and and_12 (and_12_out, B2, S3, A2);
  and and_13 (and_13_out, A2, S2, not_3_out);
  xor xor_1 (F3, and_9_out, nor_5_out);
  nor nor_5 (nor_5_out, and_11_out, and_14_out, and_15_out, and_18_out, and_18_out);
  and and_14 (and_14_out, nor_4_out, nor_7_out, nor_12_out, not_9_out, not_9_out);
  and and_15 (and_15_out, nor_4_out, nor_9_out, not_9_out);
  nor nor_6 (nor_6_out, and_16_out, and_17_out, and_19_out);
  and and_16 (and_16_out, not_3_out, S1);
  and and_17 (and_17_out, S0, B2);
  not not_3 (not_3_out, B2);
  and and_18 (and_18_out, nor_6_out, not_9_out);
  and and_19 (and_19_out, A2, A2);
  and and_20 (and_20_out, nor_4_out, not_4_out);
  and and_21 (and_21_out, nor_7_out, nor_7_out, nor_11_out, Cn, not_9_out);
  not not_4 (not_4_out, nor_6_out);
  nor nor_7 (nor_7_out, and_22_out, and_25_out);
  and and_22 (and_22_out, B1, S3, A1);
  xor xor_2 (F2, and_20_out, nor_8_out);
  nor nor_8 (nor_8_out, and_21_out, and_23_out, and_24_out);
  and and_23 (and_23_out, nor_7_out, nor_12_out, not_9_out);
  and and_24 (and_24_out, nor_9_out, not_9_out);
  and and_25 (and_25_out, A1, S2, not_5_out);
  and and_26 (and_26_out, not_5_out, S1);
  not not_5 (not_5_out, B1);
  and and_27 (A_B_3b64f046, F3, F3, F2, F1, F0);
  and and_28 (and_28_out, nor_7_out, not_6_out);
  not not_6 (not_6_out, nor_9_out);
  nor nor_9 (nor_9_out, and_26_out, and_29_out, and_30_out);
  and and_29 (and_29_out, S0, B1);
  and and_30 (and_30_out, A1, A1);
  xor xor_3 (F1, and_28_out, nor_10_out);
  and and_31 (and_31_out, Cn, nor_11_out, not_9_out);
  and and_32 (and_32_out, B0, S3, A0);
  nor nor_10 (nor_10_out, and_31_out, and_33_out);
  and and_33 (and_33_out, nor_12_out, not_9_out);
  nor nor_11 (nor_11_out, and_32_out, and_34_out);
  and and_34 (and_34_out, A0, S2, not_7_out);
  not not_7 (not_7_out, B0);
  and and_35 (and_35_out, nor_11_out, not_8_out);
  not not_8 (not_8_out, nor_12_out);
  nor nor_12 (nor_12_out, and_36_out, and_37_out, and_38_out);
  and and_36 (and_36_out, not_7_out, S1);
  and and_37 (and_37_out, S0, B0);
  xor xor_4 (F0, and_35_out, nand_4_out);
  nand nand_4 (nand_4_out, not_9_out, Cn);
  and and_38 (and_38_out, A0, A0);
  not not_9 (not_9_out, M);
endmodule
