// Logisim project alu_circuits_part1.circ as structural Verilog: 1 circuit, main circuit main
module main (
  input  input1,
  input  in_2,
  input  in_3,
  input  in_4,
  input  in_5,
  input  in_6,
  input  input2,
  input  in_8,
  input  in_9,
  input  in_10,
  input  in_11,
  input  in_12,
  input  carry,
  output out_14,
  output out_15,
  output out_16,
  output out_17,
  output out_18,
  output out_19,
  output out_20,
  output out_21,
  output out_22,
  output out_23,
  output out_24,
  output out_25
);

  wire adder_3_cout, adder_4_cout, adder_5_cout, and_2_out, and_3_out, and_4_out, xor_2_out;
  wire [3:0] adder_6_out;

  xor xor_1 (out_15, in_2, in_8);
  and and_1 (out_16, in_2, in_8);
  Adder #(.width(1)) adder_1 (.a(input1), .b(input2), .out(out_24), .cin(carry), .cout(out_25));
  and and_2 (and_2_out, input1, input2);
  and and_3 (and_3_out, input1, carry);
  and and_4 (and_4_out, input2, carry);
  xor xor_2 (xor_2_out, input1, input2);
  xor xor_3 (out_14, xor_2_out, carry);
  or or_1 (out_17, and_2_out, and_3_out, and_4_out);
  Adder #(.width(1)) adder_2 (.a(in_3), .b(in_9), .out(out_20), .cin(adder_3_cout), .cout(out_19));
  Adder #(.width(1)) adder_3 (.a(in_4), .b(in_10), .out(out_21), .cin(adder_4_cout), .cout(adder_3_cout));
  Adder #(.width(1)) adder_4 (.a(in_5), .b(in_11), .out(out_22), .cin(adder_5_cout), .cout(adder_4_cout));
  Hex_Digit_Display hex_digit_display_1 (.value({in_3, in_4, in_5, in_6}));  // open: dp
  Adder #(.width(1)) adder_5 (.a(in_6), .b(in_12), .out(out_23), .cout(adder_5_cout));  // open: cin
  Hex_Digit_Display hex_digit_display_2 (.value({in_9, in_10, in_11, in_12}));  // open: dp
  Hex_Digit_Display hex_digit_display_3 (.value({out_20, out_21, out_22, out_23}));  // open: dp
  Hex_Digit_Display hex_digit_display_4 (.value(adder_6_out));  // open: dp
  Adder #(.width(4)) adder_6 (
    .a({in_3, in_4, in_5, in_6}), .b({in_9, in_10, in_11, in_12}), .out(adder_6_out), .cout(out_18));  // open: cin

  // Notes on the sheet:
  //   Half Adder
  //   Basic ALU ops
  //   Full Adder
  //   Creating an n-bit adder from a full adder
  //   +
  //   =
endmodule
