// Logisim project alu_circuits_subtractor.circ as structural Verilog: 1 circuit, main circuit main
module main (
  input  in_1,
  input  in_2,
  input  in_3,
  input  in_4,
  input  in_5,
  input  in_6,
  input  SUB,
  output out_8,
  output out_9,
  output out_10,
  output out_11
);

  wire adder_2_cout, adder_3_cout, xor_1_out, xor_2_out, xor_3_out;

  xor xor_1 (xor_1_out, in_4, SUB);
  Adder #(.width(1)) adder_1 (.a(in_1), .b(xor_1_out), .out(out_9), .cin(adder_2_cout), .cout(out_8));
  xor xor_2 (xor_2_out, in_5, SUB);
  Adder #(.width(1)) adder_2 (.a(in_2), .b(xor_2_out), .out(out_10), .cin(adder_3_cout), .cout(adder_2_cout));
  xor xor_3 (xor_3_out, in_6, SUB);
  Adder #(.width(1)) adder_3 (.a(in_3), .b(xor_3_out), .out(out_11), .cin(SUB), .cout(adder_3_cout));
endmodule
