// Logisim project alu_ttl.circ as structural Verilog: 1 circuit, main circuit main
module main (
  input  [3:0] in_1,
  input  [3:0] in_2,
  input  in_3,
  input  in_4,
  input  in_5,
  input  in_6,
  input  in_7,
  input  in_8,
  output [3:0] out_9
);

  wire n74181_1_p1, n74181_1_p2, n74181_1_p3, n74181_1_p4, n74181_1_p6, n74181_1_p8, n74181_1_p10,
       n74181_1_p12, n74181_1_p15, n74181_1_p16, n74181_1_p17, n74181_1_p18;

  // _74181 74181_1: pin names not known; wires that end beside it: n74181_1_p1, n74181_1_p2, n74181_1_p3, n74181_1_p4, in_6, n74181_1_p6, in_5, n74181_1_p8, in_4, n74181_1_p10, in_3, n74181_1_p12, in_7, in_8, n74181_1_p15, n74181_1_p16, n74181_1_p17, n74181_1_p18
  not not_1 (n74181_1_p1, in_2[0]);
  not not_2 (n74181_1_p2, in_1[1]);
  not not_3 (n74181_1_p4, in_2[1]);
  not not_4 (n74181_1_p6, in_1[2]);
  not not_5 (n74181_1_p8, in_2[2]);
  not not_6 (n74181_1_p3, in_1[0]);
  not not_7 (n74181_1_p10, in_1[3]);
  not not_8 (n74181_1_p12, in_2[3]);
  not not_9 (out_9[3], n74181_1_p18);
  not not_10 (out_9[2], n74181_1_p17);
  not not_11 (out_9[1], n74181_1_p16);
  not not_12 (out_9[0], n74181_1_p15);
endmodule
