// Logisim project buses.circ as structural Verilog: 1 circuit, main circuit main
module main (
  input  in_1,
  input  in_2,
  input  in_3,
  input  in_4,
  input  in_5,
  input  in_6,
  input  in_7,
  input  in_8,
  input  in_9,
  input  in_10,
  input  main_clock,
  input  in_12,
  output out_13,
  output out_14,
  output out_15,
  output out_16
);

  wire [3:0] adder_1_out, register_1_q;

  Register #(.width(4)) register_1 (
    .D({out_13, out_14, out_15, out_16}), .en(in_10), .clk(main_clock), .Q(register_1_q));  // open: clr
  assign {out_13, out_14, out_15, out_16} = in_12 ? register_1_q : 4'bz;  // Controlled_Buffer controlled_buffer_1
  assign {out_13, out_14, out_15, out_16} = in_9 ? adder_1_out : 4'bz;  // Controlled_Buffer controlled_buffer_2
  Adder #(.width(4)) adder_1 (
    .a({in_1, in_2, in_3, in_4}), .b({in_5, in_6, in_7, in_8}), .out(adder_1_out));  // open: cin, cout
  Hex_Digit_Display hex_digit_display_1 ();  // open: value, dp
endmodule
