// Logisim project counters.circ as structural Verilog: 1 circuit, main circuit main
module main (
  input  in_1,
  input  in_2,
  input  clock,
  input  clock_2,
  input  in_5,
  input  JK_ring_counter,
  input  UP,
  input  in_8,
  input  in_9,
  input  in_10,
  input  in_11,
  input  in_12,
  input  in_13,
  input  in_14,
  input  in_15,
  input  in_16,
  input  in_17,
  input  in_18,
  input  in_19,
  input  in_20,
  input  in_21,
  input  in_22,
  input  in_23,
  output out_24
);

  wire and_1_out, and_2_out, and_3_out, and_4_out, and_5_out, d_ff_1_q, d_ff_2_q, d_ff_3_q, d_ff_4_q,
       j_k_ff_10_q, j_k_ff_10_qn, j_k_ff_13_q, j_k_ff_13_qn, j_k_ff_15_q, j_k_ff_15_qn, j_k_ff_16_q,
       j_k_ff_16_qn, j_k_ff_25_qn, j_k_ff_26_qn, j_k_ff_28_qn, nand_1_out, nand_2_out, nand_3_out,
       nand_4_out, nand_5_out, nand_6_out, nand_7_out, nand_8_out, nand_9_out, nand_10_out, nand_11_out,
       nand_12_out, nand_13_out, nand_14_out, nand_15_out, nand_16_out, nand_17_out, nand_18_out,
       nand_19_out, nand_20_out, nand_21_out, nand_22_out, not_1_out, not_2_out, not_3_out, not_4_out,
       not_5_out, not_6_out, not_7_out, not_8_out, not_9_out, not_10_out, not_11_out, not_12_out, not_13_out,
       not_14_out, not_15_out, not_16_out, not_17_out, not_18_out, not_19_out, not_20_out, not_21_out,
       not_22_out, not_23_out, not_24_out, not_25_out, or_1_out, or_2_out, or_3_out, or_4_out;
  wire [3:0] j_k_ff_6_q, j_k_ff_8_q, j_k_ff_14_q, j_k_ff_24_q, j_k_ff_27_q, j_k_ff_28_q;

  J_K_Flip_Flop #(.trigger("falling")) j_k_ff_1 (
    .J(in_1), .K(in_1), .clk(j_k_ff_6_q[2]), .Q(j_k_ff_6_q[3]));  // open: Qn, preset, reset
  LED led_1 (.in(j_k_ff_6_q[3]));
  J_K_Flip_Flop #(.trigger("falling")) j_k_ff_2 (
    .J(in_1), .K(in_1), .clk(j_k_ff_6_q[1]), .Q(j_k_ff_6_q[2]));  // open: Qn, preset, reset
  LED led_2 (.in(j_k_ff_6_q[2]));
  D_Flip_Flop d_ff_1 (.D(d_ff_2_q), .clk(in_8), .Q(d_ff_1_q), .reset(in_9));  // open: Qn, preset
  not not_1 (not_1_out, in_12);
  nand nand_1 (nand_1_out, in_12, in_16);
  nand nand_2 (nand_2_out, not_1_out, in_16);
  not not_2 (not_2_out, nand_1_out);
  J_K_Flip_Flop #(.trigger("falling")) j_k_ff_3 (
    .J(1'b1), .K(1'b1), .clk(j_k_ff_8_q[2]), .Q(j_k_ff_8_q[3]), .preset(not_2_out), .reset(not_3_out));  // open: Qn
  not not_3 (not_3_out, nand_2_out);
  J_K_Flip_Flop #(.trigger("falling")) j_k_ff_4 (
    .J(in_1), .K(in_1), .clk(j_k_ff_6_q[0]), .Q(j_k_ff_6_q[1]));  // open: Qn, preset, reset
  D_Flip_Flop d_ff_2 (.D(d_ff_3_q), .clk(in_8), .Q(d_ff_2_q), .reset(in_9));  // open: Qn, preset
  J_K_Flip_Flop #(.trigger("falling")) j_k_ff_5 (
    .J(1'b1), .K(1'b1), .clk(j_k_ff_8_q[1]), .Q(j_k_ff_8_q[2]), .preset(not_5_out), .reset(not_6_out));  // open: Qn
  LED led_3 (.in(j_k_ff_6_q[1]));
  D_Flip_Flop d_ff_3 (.D(d_ff_4_q), .clk(in_8), .Q(d_ff_3_q), .reset(in_9));  // open: Qn, preset
  not not_4 (not_4_out, in_13);
  nand nand_3 (nand_3_out, in_13, in_16);
  nand nand_4 (nand_4_out, not_4_out, in_16);
  not not_5 (not_5_out, nand_3_out);
  not not_6 (not_6_out, nand_4_out);
  J_K_Flip_Flop #(.trigger("falling")) j_k_ff_6 (
    .J(in_1), .K(in_1), .clk(in_2), .Q(j_k_ff_6_q[0]));  // open: Qn, preset, reset
  LED led_4 (.in(j_k_ff_6_q[0]));
  LedBar #(.matrixcols(4)) ledbar_1 (.led0(d_ff_1_q), .led1(d_ff_2_q), .led2(d_ff_3_q), .led3(d_ff_4_q));
  nand nand_5 (nand_5_out, in_14, in_16);
  not not_7 (not_7_out, nand_5_out);
  J_K_Flip_Flop #(.trigger("falling")) j_k_ff_7 (
    .J(1'b1), .K(1'b1), .clk(j_k_ff_8_q[0]), .Q(j_k_ff_8_q[1]), .preset(not_7_out), .reset(not_8_out));  // open: Qn
  not not_8 (not_8_out, nand_6_out);
  Hex_Digit_Display hex_digit_display_1 (.value(j_k_ff_6_q));  // open: dp
  D_Flip_Flop d_ff_4 (.D(d_ff_1_q), .clk(in_8), .Q(d_ff_4_q), .preset(in_9));  // open: Qn, reset
  not not_9 (not_9_out, in_14);
  nand nand_6 (nand_6_out, not_9_out, in_16);
  Controlled_Buffer controlled_buffer_1 ();  // open: in, out, en
  not not_10 (not_10_out, in_15);
  nand nand_7 (nand_7_out, in_15, in_16);
  nand nand_8 (nand_8_out, not_10_out, in_16);
  not not_11 (not_11_out, nand_7_out);
  J_K_Flip_Flop #(.trigger("falling")) j_k_ff_8 (
    .J(1'b1), .K(1'b1), .clk(in_22), .Q(j_k_ff_8_q[0]), .preset(not_11_out), .reset(not_12_out));  // open: Qn
  not not_12 (not_12_out, nand_8_out);
  Hex_Digit_Display hex_digit_display_2 (.value(j_k_ff_8_q));  // open: dp
  and and_1 (and_1_out, j_k_ff_14_q[2], and_2_out);
  J_K_Flip_Flop j_k_ff_9 (.J(and_1_out), .K(and_1_out), .clk(clock), .Q(j_k_ff_14_q[3]));  // open: Qn, preset, reset
  LED led_5 (.in(j_k_ff_14_q[3]));
  J_K_Flip_Flop #(.trigger("falling")) j_k_ff_10 (
    .J(j_k_ff_13_q), .K(j_k_ff_13_qn), .clk(JK_ring_counter), .Q(j_k_ff_10_q), .Qn(j_k_ff_10_qn),
    .reset(in_10));  // open: preset
  and and_2 (and_2_out, j_k_ff_14_q[0], j_k_ff_14_q[1]);
  J_K_Flip_Flop j_k_ff_11 (.J(and_2_out), .K(and_2_out), .clk(clock), .Q(j_k_ff_14_q[2]));  // open: Qn, preset, reset
  LED led_6 (.in(j_k_ff_14_q[2]));
  J_K_Flip_Flop j_k_ff_12 (
    .J(j_k_ff_14_q[0]), .K(j_k_ff_14_q[0]), .clk(clock), .Q(j_k_ff_14_q[1]));  // open: Qn, preset, reset
  LED led_7 (.in(j_k_ff_14_q[1]));
  J_K_Flip_Flop #(.trigger("falling")) j_k_ff_13 (
    .J(j_k_ff_15_q), .K(j_k_ff_15_qn), .clk(JK_ring_counter), .Q(j_k_ff_13_q), .Qn(j_k_ff_13_qn),
    .reset(in_10));  // open: preset
  J_K_Flip_Flop j_k_ff_14 (.J(1'b1), .K(1'b1), .clk(clock), .Q(j_k_ff_14_q[0]));  // open: Qn, preset, reset
  LED led_8 (.in(j_k_ff_14_q[0]));
  J_K_Flip_Flop #(.trigger("falling")) j_k_ff_15 (
    .J(j_k_ff_16_qn), .K(j_k_ff_16_q), .clk(JK_ring_counter), .Q(j_k_ff_15_q), .Qn(j_k_ff_15_qn),
    .reset(in_10));  // open: preset
  LedBar #(.matrixcols(4)) ledbar_2 (.led0(j_k_ff_10_q), .led1(j_k_ff_13_q), .led2(j_k_ff_15_q), .led3(j_k_ff_16_qn));
  Hex_Digit_Display hex_digit_display_3 (.value(j_k_ff_14_q));  // open: dp
  J_K_Flip_Flop #(.trigger("falling")) j_k_ff_16 (
    .J(j_k_ff_10_qn), .K(j_k_ff_10_q), .clk(JK_ring_counter), .Q(j_k_ff_16_q), .Qn(j_k_ff_16_qn),
    .reset(in_10));  // open: preset
  or or_1 (or_1_out, in_5, and_5_out);
  nand nand_9 (nand_9_out, in_17, in_21);
  not not_13 (not_13_out, nand_9_out);
  J_K_Flip_Flop #(.trigger("falling")) j_k_ff_17 (
    .J(1'b1), .K(1'b1), .clk(j_k_ff_27_q[2]), .Q(j_k_ff_27_q[3]), .preset(not_13_out), .reset(not_14_out));  // open: Qn
  not not_14 (not_14_out, nand_10_out);
  and and_3 (and_3_out, j_k_ff_24_q[2], and_4_out);
  J_K_Flip_Flop j_k_ff_18 (
    .J(and_3_out), .K(and_3_out), .clk(clock_2), .Q(j_k_ff_24_q[3]), .reset(or_1_out));  // open: Qn, preset
  LED led_9 (.in(j_k_ff_24_q[3]));
  not not_15 (not_15_out, in_17);
  nand nand_10 (nand_10_out, not_15_out, in_21);
  and and_4 (and_4_out, j_k_ff_24_q[0], j_k_ff_24_q[1]);
  J_K_Flip_Flop j_k_ff_19 (
    .J(and_4_out), .K(and_4_out), .clk(clock_2), .Q(j_k_ff_24_q[2]), .reset(or_1_out));  // open: Qn, preset
  LED led_10 (.in(j_k_ff_24_q[2]));
  nand nand_11 (nand_11_out, in_18, in_21);
  not not_16 (not_16_out, nand_11_out);
  J_K_Flip_Flop #(.trigger("falling")) j_k_ff_20 (
    .J(1'b1), .K(1'b1), .clk(j_k_ff_27_q[1]), .Q(j_k_ff_27_q[2]), .preset(not_16_out), .reset(not_17_out));  // open: Qn
  not not_17 (not_17_out, nand_12_out);
  J_K_Flip_Flop j_k_ff_21 (
    .J(j_k_ff_24_q[0]), .K(j_k_ff_24_q[0]), .clk(clock_2), .Q(j_k_ff_24_q[1]), .reset(or_1_out));  // open: Qn, preset
  J_K_Flip_Flop #(.trigger("falling")) j_k_ff_22 (
    .J(1'b1), .K(1'b1), .clk(or_2_out), .Q(j_k_ff_28_q[3]));  // open: Qn, preset, reset
  not not_18 (not_18_out, in_18);
  nand nand_12 (nand_12_out, not_18_out, in_21);
  LED led_11 (.in(j_k_ff_24_q[1]));
  nand nand_13 (nand_13_out, in_19, in_21);
  not not_19 (not_19_out, nand_13_out);
  J_K_Flip_Flop #(.trigger("falling")) j_k_ff_23 (
    .J(1'b1), .K(1'b1), .clk(j_k_ff_27_q[0]), .Q(j_k_ff_27_q[1]), .preset(not_19_out), .reset(not_20_out));  // open: Qn
  not not_20 (not_20_out, nand_16_out);
  J_K_Flip_Flop j_k_ff_24 (
    .J(1'b1), .K(1'b1), .clk(clock_2), .Q(j_k_ff_24_q[0]), .reset(or_1_out));  // open: Qn, preset
  LED led_12 (.in(j_k_ff_24_q[0]));
  nand nand_14 (nand_14_out, UP, j_k_ff_28_q[2]);
  nand nand_15 (nand_15_out, not_25_out, j_k_ff_25_qn);
  or or_2 (or_2_out, ~nand_14_out, ~nand_15_out);  // OR_Gate
  J_K_Flip_Flop #(.trigger("falling")) j_k_ff_25 (
    .J(1'b1), .K(1'b1), .clk(or_3_out), .Q(j_k_ff_28_q[2]), .Qn(j_k_ff_25_qn));  // open: preset, reset
  not not_21 (not_21_out, in_19);
  nand nand_16 (nand_16_out, not_21_out, in_21);
  and and_5 (and_5_out, j_k_ff_24_q[3], ~j_k_ff_24_q[2], j_k_ff_24_q[1], j_k_ff_24_q[0]);  // AND_Gate
  Hex_Digit_Display hex_digit_display_4 (.value(j_k_ff_24_q));  // open: dp
  nand nand_17 (nand_17_out, UP, j_k_ff_28_q[1]);
  J_K_Flip_Flop #(.trigger("falling")) j_k_ff_26 (
    .J(1'b1), .K(1'b1), .clk(or_4_out), .Q(j_k_ff_28_q[1]), .Qn(j_k_ff_26_qn));  // open: preset, reset
  nand nand_18 (nand_18_out, in_20, in_21);
  J_K_Flip_Flop #(.trigger("falling")) j_k_ff_27 (
    .J(1'b1), .K(1'b1), .clk(in_23), .Q(j_k_ff_27_q[0]), .preset(not_23_out), .reset(not_24_out));  // open: Qn
  Hex_Digit_Display hex_digit_display_5 (.value(j_k_ff_27_q));  // open: dp
  nand nand_19 (nand_19_out, not_25_out, j_k_ff_26_qn);
  or or_3 (or_3_out, ~nand_17_out, ~nand_19_out);  // OR_Gate
  Hex_Digit_Display hex_digit_display_6 (.value(j_k_ff_28_q));  // open: dp
  not not_22 (not_22_out, in_20);
  nand nand_20 (nand_20_out, not_22_out, in_21);
  not not_23 (not_23_out, nand_18_out);
  not not_24 (not_24_out, nand_20_out);
  nand nand_21 (nand_21_out, UP, j_k_ff_28_q[0]);
  nand nand_22 (nand_22_out, not_25_out, j_k_ff_28_qn);
  or or_4 (or_4_out, ~nand_21_out, ~nand_22_out);  // OR_Gate
  J_K_Flip_Flop #(.trigger("falling")) j_k_ff_28 (
    .J(1'b1), .K(1'b1), .clk(in_11), .Q(j_k_ff_28_q[0]), .Qn(j_k_ff_28_qn));  // open: preset, reset
  not not_25 (not_25_out, UP);
  nor nor_1 (out_24, j_k_ff_27_q[0], j_k_ff_27_q[1], j_k_ff_27_q[2], j_k_ff_27_q[3]);

  // Notes on the sheet:
  //   ripple counter
  //   Ring Counters
  //   presettable-counter
  //   COUNT DOWN
  //   Synchronous Counter
  //   load
  //   This 'LOAD' needs to be an edge detected switch
  //   programmable counter
  //   clr
  //   Mod 10 counter
  //   up down counter
  //   load
endmodule
