// Logisim project memories.circ as structural Verilog: 1 circuit, main circuit main
module main (
  input  [7:0] in_1,
  input  [7:0] in_2,
  input  in_3,
  input  in_4,
  input  in_5,
  input  [7:0] in_6,
  output [7:0] out_7,
  output [7:0] out_8
);

  ROM rom_1 (.addr(in_2), .data(out_7));
  RAM ram_1 (.addr(in_1), .we(in_3), .oe(in_4), .clk(in_5), .din(in_6), .dout(out_8));

  // Notes on the sheet:
  //   contents of rom_1 (hex, n*v repeats v):
  //   0 1f
endmodule
