// Logisim project registers.circ as structural Verilog: 1 circuit, main circuit main
module main (
  input  in_1,
  input  in_2,
  input  in_3,
  input  in_4,
  input  in_5,
  input  in_6,
  input  in_7,
  input  in_8,
  input  in_9,
  input  in_10,
  input  in_11,
  input  in_12,
  input  in_13,
  input  in_14,
  input  CLR,
  input  in_16,
  input  CLR_2,
  output out_18,
  output out_19,
  output out_20,
  output out_21,
  output out_22,
  output out_23,
  output out_24,
  output out_25
);

  wire and_1_out, and_2_out, and_3_out, and_4_out, and_5_out, and_6_out, and_7_out, and_8_out, clock_1_out,
       clock_2_out, not_1_out, or_1_out, or_2_out, or_3_out, or_4_out;
  wire [3:0] register_1_q;

  D_Flip_Flop d_ff_1 (.D(in_1), .clk(in_16), .Q(out_18), .reset(CLR));  // open: Qn, preset
  D_Flip_Flop d_ff_2 (.D(in_2), .clk(in_16), .Q(out_19), .reset(CLR));  // open: Qn, preset
  D_Flip_Flop d_ff_3 (.D(in_3), .clk(in_16), .Q(out_20), .reset(CLR));  // open: Qn, preset
  D_Flip_Flop d_ff_4 (.D(in_4), .clk(in_16), .Q(out_21), .reset(CLR));  // open: Qn, preset
  Clock clock_1 (.out(clock_1_out));
  and and_1 (and_1_out, in_9, in_13);
  and and_2 (and_2_out, not_1_out, out_22);
  or or_1 (or_1_out, and_1_out, and_2_out);
  D_Flip_Flop d_ff_5 (.D(or_1_out), .clk(clock_1_out), .Q(out_22), .reset(CLR_2));  // open: Qn, preset
  and and_3 (and_3_out, in_12, in_13);
  and and_4 (and_4_out, not_1_out, out_23);
  or or_2 (or_2_out, and_3_out, and_4_out);
  D_Flip_Flop d_ff_6 (.D(or_2_out), .clk(clock_1_out), .Q(out_23), .reset(CLR_2));  // open: Qn, preset
  and and_5 (and_5_out, in_10, in_13);
  and and_6 (and_6_out, not_1_out, out_24);
  or or_3 (or_3_out, and_5_out, and_6_out);
  D_Flip_Flop d_ff_7 (.D(or_3_out), .clk(clock_1_out), .Q(out_24), .reset(CLR_2));  // open: Qn, preset
  and and_7 (and_7_out, in_11, in_13);
  not not_1 (not_1_out, in_13);
  and and_8 (and_8_out, not_1_out, out_25);
  or or_4 (or_4_out, and_7_out, and_8_out);
  D_Flip_Flop d_ff_8 (.D(or_4_out), .clk(clock_1_out), .Q(out_25), .reset(CLR_2));  // open: Qn, preset
  Hex_Digit_Display hex_digit_display_1 (.value({out_22, out_23, out_24, out_25}));  // open: dp
  Hex_Digit_Display hex_digit_display_2 (.value({in_9, in_12, in_10, in_11}));  // open: dp
  Clock clock_2 (.out(clock_2_out));
  Hex_Digit_Display hex_digit_display_3 (.value({in_5, in_6, in_7, in_8}));  // open: dp
  Register #(.width(4)) register_1 (
    .D({in_5, in_6, in_7, in_8}), .en(in_14), .clk(clock_2_out), .Q(register_1_q));  // open: clr
  Hex_Digit_Display hex_digit_display_4 (.value(register_1_q));  // open: dp

  // Notes on the sheet:
  //   Basic Buffer Register
  //   CLK
  //   Controlled Buffer Register
  //   CLK
  //   LOAD
endmodule
