// Logisim project sap1.circ as structural Verilog: 1 circuit, main circuit main
module main (
  input  in_1,
  input  [11:0] in_2,
  input  [11:0] in_3,
  input  [11:0] in_4,
  input  [11:0] in_5,
  input  [11:0] in_6,
  input  in_7,
  input  [11:0] in_8,
  input  [11:0] in_9,
  input  [11:0] in_10,
  input  [11:0] in_11,
  input  [11:0] in_12,
  input  [11:0] in_13,
  input  [11:0] in_14,
  input  [11:0] in_15,
  input  [11:0] in_16,
  input  [11:0] in_17,
  output out_18,
  output out_19,
  output out_20,
  output out_21,
  output out_22,
  output out_23,
  output out_24,
  output out_25,
  output [7:0] out_26,
  output [7:0] out_27,
  output out_28,
  output out_29,
  output out_30,
  output out_31,
  output out_32,
  output out_33,
  output out_34,
  output out_35,
  output out_36,
  output out_37,
  output out_38,
  output out_39,
  output [11:0] out_40,
  output [11:0] out_41,
  output [11:0] out_42
);

  wire and_3_out, and_4_out, clock_1_out, controlled_buffer_6_out, controlled_buffer_7_out, not_1_out,
       not_2_out, not_3_out, not_4_out, not_5_out, not_6_out, not_7_out, not_8_out, undriven;
  wire [2:0] counter_2_q;
  wire [3:0] counter_1_q, counter_3_q, register_1_q, register_2_q, register_2_q_2, rom_1_data;
  wire [7:0] adder_1_out, and_1_out, and_2_out, or_1_out, register_3_q, register_4_q;
  wire [11:0] multiplexer_1_out, multiplexer_2_out, multiplexer_3_out, multiplexer_4_out;

  Clock clock_1 (.out(clock_1_out));
  RAM #(.addrWidth(4), .trigger("falling"), .\type ("nonvolatile")) ram_1 (
    .addr(register_1_q), .oe(in_1), .clk(clock_1_out), .dout(out_26));  // open: we, din
  not not_1 (not_1_out, out_30);
  not not_2 (not_2_out, out_31);
  not not_3 (not_3_out, out_32);
  not not_4 (not_4_out, out_33);
  Counter #(.max('hf), .width(4)) counter_1 (
    .count(out_28), .clk(clock_1_out), .Q(counter_1_q));  // open: clr, load, up, D, carry
  Register #(.width(4)) register_1 (
    .D({out_22, out_23, out_24, out_25}), .en(not_1_out), .clk(clock_1_out), .Q(register_1_q));  // open: clr
  Register register_2 (
    .D({out_18, out_19, out_20, out_21, out_22, out_23, out_24, out_25}), .en(not_3_out), .clk(clock_1_out),
    .Q({register_2_q_2, register_2_q}));  // open: clr
  assign {out_18, out_19, out_20, out_21, out_22, out_23, out_24, out_25} = not_4_out ? {register_2_q_2, register_2_q} : 8'bz;  // Controlled_Buffer controlled_buffer_1
  assign {out_22, out_23, out_24, out_25} = out_29 ? counter_1_q : 4'bz;  // Controlled_Buffer controlled_buffer_2
  assign {out_18, out_19, out_20, out_21, out_22, out_23, out_24, out_25} = not_2_out ? out_26 : 8'bz;  // Controlled_Buffer controlled_buffer_3
  Multiplexer #(.select(3), .width(12)) multiplexer_1 (
    .in0(in_8), .in1(in_13), .in2(in_14), .in3(multiplexer_2_out), .in4(multiplexer_3_out),
    .in5(multiplexer_4_out), .out(multiplexer_1_out), .sel(counter_2_q));  // open: in6, in7
  Counter #(.max('h5), .width(3)) counter_2 (
    .count(undriven), .clk(clock_1_out), .Q(counter_2_q));  // open: clr, load, up, D, carry
  assign {out_18, out_19, out_20, out_21, out_22, out_23, out_24, out_25} = out_35 ? register_3_q : 8'bz;  // Controlled_Buffer controlled_buffer_4
  assign {out_18, out_19, out_20, out_21, out_22, out_23, out_24, out_25} = out_37 ? adder_1_out : 8'bz;  // Controlled_Buffer controlled_buffer_5
  Register register_3 (
    .D({out_18, out_19, out_20, out_21, out_22, out_23, out_24, out_25}), .en(not_6_out), .clk(clock_1_out),
    .Q(register_3_q));  // open: clr
  Register register_4 (
    .D({out_18, out_19, out_20, out_21, out_22, out_23, out_24, out_25}), .en(not_8_out), .clk(clock_1_out),
    .Q(register_4_q));  // open: clr
  Register register_5 (
    .D({out_18, out_19, out_20, out_21, out_22, out_23, out_24, out_25}), .en(not_7_out), .clk(clock_1_out),
    .Q(out_27));  // open: clr
  Adder adder_1 (.a(register_3_q), .b(or_1_out), .out(adder_1_out), .cin(out_36));  // open: cout
  assign or_1_out = and_1_out | and_2_out;  // OR_Gate or_1, 8 bits wide
  assign and_1_out = register_4_q & ~{8{out_36}};  // AND_Gate and_1, 8 bits wide
  assign and_2_out = ~register_4_q & {8{out_36}};  // AND_Gate and_2, 8 bits wide
  Multiplexer #(.select(4), .width(12)) multiplexer_2 (
    .in0(in_4), .in1(in_9), .in2(in_12), .in14(in_17), .out(multiplexer_2_out), .sel(register_2_q_2));  // open: in3, in4, in5, in6, in7, in8, in9, in10, in11, in12, in13, in15
  Hex_Digit_Display hex_digit_display_1 (.value(out_27[7:4]));  // open: dp
  Hex_Digit_Display hex_digit_display_2 (.value(out_27[3:0]));  // open: dp
  not not_5 (not_5_out, counter_2_q[2]);
  Multiplexer #(.select(4), .width(12)) multiplexer_3 (
    .in0(in_2), .in1(in_5), .in2(in_10), .in14(in_15), .out(multiplexer_3_out), .sel(register_2_q_2));  // open: in3, in4, in5, in6, in7, in8, in9, in10, in11, in12, in13, in15
  and and_3 (and_3_out, counter_2_q[0], counter_2_q[1], not_5_out);
  and and_4 (and_4_out, ~counter_2_q[0], ~counter_2_q[1], ~counter_2_q[2]);  // AND_Gate
  not not_6 (not_6_out, out_34);
  not not_7 (not_7_out, out_39);
  ROM #(.addrWidth(4), .dataWidth(4)) rom_1 (.addr(register_2_q_2), .data(rom_1_data));
  assign controlled_buffer_6_out = clock_1_out ? and_3_out : 1'bz;  // Controlled_Buffer controlled_buffer_6
  assign controlled_buffer_7_out = clock_1_out ? and_4_out : 1'bz;  // Controlled_Buffer controlled_buffer_7
  not not_8 (not_8_out, out_38);
  Multiplexer #(.select(4), .width(12)) multiplexer_4 (
    .in0(in_3), .in1(in_6), .in2(in_11), .in14(in_16), .out(multiplexer_4_out), .sel(register_2_q_2));  // open: in3, in4, in5, in6, in7, in8, in9, in10, in11, in12, in13, in15
  Counter #(.max('hf), .trigger("falling"), .width(4)) counter_3 (
    .clr(controlled_buffer_7_out), .load(controlled_buffer_6_out), .clk(clock_1_out), .D(rom_1_data),
    .Q(counter_3_q));  // open: up, count, carry
  ROM #(.addrWidth(4), .dataWidth(12)) rom_2 (
    .addr(counter_3_q),
    .data({out_28, out_29, out_30, out_31, out_32, out_33, out_34, out_35, out_36, out_37, out_38, out_39}));

  assign out_40 = {out_28, out_29, out_30, out_31, out_32, out_33, out_34, out_35, out_36, out_37, out_38, out_39};
  assign out_41 = {out_28, out_29, out_30, out_31, out_32, out_33, out_34, out_35, out_36, out_37, out_38, out_39};
  assign out_42 = {out_28, out_29, out_30, out_31, out_32, out_33, out_34, out_35, out_36, out_37, out_38, out_39};

  // Notes on the sheet:
  //   in_4: initial=0x1a3
  //   in_9: initial=0x1a3
  //   in_12: initial=0x1a3
  //   in_17: initial=0x3f2
  //   in_5: initial=0x2e1
  //   in_10: initial=0x2e1
  //   in_15: initial=0x3e3
  //   in_3: initial=0x3e3
  //   in_2: initial=0x2c3
  //   in_6: initial=0x3c7
  //   in_11: initial=0x3cf
  //   in_16: initial=0x3e3
  //   in_1: initial=0x1
  //   in_8: initial=0x5e3
  //   in_13: initial=0xbe3
  //   in_14: initial=0x263
  //   Cp
  //   Ep
  //   Lm^
  //   CpEpLm.CE. 
  //   La^
  //   Ea
  //   Su
  //   CE^
  //   Li^
  //   Ei^
  //   Li.Ei.La.Ea
  //   Eu
  //   Lb^
  //   Lo^
  //   SuEuLb.Lo.
  //   OLD control box
  //   FETCH CYCLE
  //   Instruction Bits
  //   contents of rom_1 (hex, n*v repeats v):
  //   3 6 9 11*0 c
  //   contents of rom_2 (hex, n*v repeats v):
  //   5e3 be3 263 1a3 2c3 3e3 1a3 2e1 3c7 1a3 2e1 3cf 3f2 3e3 3e3
endmodule
