// Logisim project sap1_rom_control.circ as structural Verilog: 1 circuit, main circuit main
module main (
  input  in_1,
  input  [1:0] in_2,
  output out_3,
  output out_4,
  output out_5,
  output out_6,
  output out_7,
  output out_8,
  output out_9,
  output out_10,
  output [7:0] out_11,
  output [15:0] out_12,
  output [7:0] out_13,
  output out_14,
  output out_15,
  output out_16,
  output out_17,
  output out_18,
  output out_19,
  output out_20,
  output out_21,
  output out_22,
  output out_23,
  output out_24,
  output out_25,
  output [11:0] out_26
);

  wire and_1_out, and_4_out, and_5_out, clock_1_out, comparator_1_eq, controlled_buffer_6_out,
       controlled_buffer_7_out, counter_1_carry, counter_4_carry, not_1_out, not_2_out, not_3_out, not_4_out,
       not_5_out, not_6_out, not_7_out, not_8_out;
  wire [2:0] counter_2_q;
  wire [3:0] counter_1_q, counter_3_q, register_1_q, register_2_q, register_2_q_2, rom_2_data;
  wire [7:0] adder_1_out, and_2_out, and_3_out, or_1_out, register_3_q, register_4_q;
  wire [11:0] rom_1_data;

  Clock clock_1 (.out(clock_1_out));
  and and_1 (and_1_out, ~counter_1_carry, clock_1_out);  // AND_Gate
  RAM #(.addrWidth(4), .trigger("falling"), .\type ("nonvolatile")) ram_1 (
    .addr(register_1_q), .oe(in_1), .clk(and_1_out), .dout(out_11));  // open: we, din
  not not_1 (not_1_out, out_16);
  not not_2 (not_2_out, out_17);
  not not_3 (not_3_out, out_18);
  not not_4 (not_4_out, out_19);
  Counter #(.max('hf), .width(4)) counter_1 (
    .count(out_14), .clk(and_1_out), .carry(counter_1_carry), .Q(counter_1_q));  // open: clr, load, up, D
  Register #(.width(4)) register_1 (
    .D({out_7, out_8, out_9, out_10}), .en(not_1_out), .clk(and_1_out), .Q(register_1_q));  // open: clr
  Register register_2 (
    .D({out_3, out_4, out_5, out_6, out_7, out_8, out_9, out_10}), .en(not_3_out), .clk(and_1_out),
    .Q({register_2_q_2, register_2_q}));  // open: clr
  assign {out_3, out_4, out_5, out_6, out_7, out_8, out_9, out_10} = not_4_out ? {register_2_q_2, register_2_q} : 8'bz;  // Controlled_Buffer controlled_buffer_1
  assign {out_7, out_8, out_9, out_10} = out_15 ? counter_1_q : 4'bz;  // Controlled_Buffer controlled_buffer_2
  assign {out_3, out_4, out_5, out_6, out_7, out_8, out_9, out_10} = not_2_out ? out_11 : 8'bz;  // Controlled_Buffer controlled_buffer_3
  ROM #(.addrWidth(2), .dataWidth(12)) rom_1 (.addr(in_2), .data(rom_1_data));
  assign {out_3, out_4, out_5, out_6, out_7, out_8, out_9, out_10} = out_21 ? register_3_q : 8'bz;  // Controlled_Buffer controlled_buffer_4
  assign {out_3, out_4, out_5, out_6, out_7, out_8, out_9, out_10} = out_23 ? adder_1_out : 8'bz;  // Controlled_Buffer controlled_buffer_5
  Register register_3 (
    .D({out_3, out_4, out_5, out_6, out_7, out_8, out_9, out_10}), .en(not_6_out), .clk(and_1_out),
    .Q(register_3_q));  // open: clr
  Register register_4 (
    .D({out_3, out_4, out_5, out_6, out_7, out_8, out_9, out_10}), .en(not_8_out), .clk(and_1_out),
    .Q(register_4_q));  // open: clr
  Register register_5 (
    .D({out_3, out_4, out_5, out_6, out_7, out_8, out_9, out_10}), .en(not_7_out), .clk(and_1_out), .Q(out_13));  // open: clr
  Adder adder_1 (.a(register_3_q), .b(or_1_out), .out(adder_1_out), .cin(out_22));  // open: cout
  assign or_1_out = and_2_out | and_3_out;  // OR_Gate or_1, 8 bits wide
  assign and_2_out = register_4_q & ~{8{out_22}};  // AND_Gate and_2, 8 bits wide
  assign and_3_out = ~register_4_q & {8{out_22}};  // AND_Gate and_3, 8 bits wide
  Hex_Digit_Display hex_digit_display_1 (.value(out_13[7:4]));  // open: dp
  ROM #(.addrWidth(4), .dataWidth(4)) rom_2 (.addr(register_2_q_2), .data(rom_2_data));
  Counter #(.max('h5), .width(3)) counter_2 (.clk(and_1_out), .Q(counter_2_q));  // open: clr, load, up, count, D, carry
  Hex_Digit_Display hex_digit_display_2 (.value(out_13[3:0]));  // open: dp
  not not_5 (not_5_out, counter_2_q[2]);
  Comparator #(.width(12)) comparator_1 (
    .a(rom_1_data),
    .b({out_14, out_15, out_16, out_17, out_18, out_19, out_20, out_21, out_22, out_23, out_24, out_25}),
    .eq(comparator_1_eq));  // open: gt, lt
  and and_4 (and_4_out, counter_2_q[0], counter_2_q[1], not_5_out);
  and and_5 (and_5_out, ~counter_2_q[0], ~counter_2_q[1], ~counter_2_q[2]);  // AND_Gate
  assign controlled_buffer_6_out = and_1_out ? and_5_out : 1'bz;  // Controlled_Buffer controlled_buffer_6
  not not_6 (not_6_out, out_20);
  not not_7 (not_7_out, out_25);
  assign controlled_buffer_7_out = and_1_out ? and_4_out : 1'bz;  // Controlled_Buffer controlled_buffer_7
  not not_8 (not_8_out, out_24);
  Counter #(.max('hf), .trigger("falling"), .width(4)) counter_3 (
    .clr(controlled_buffer_6_out), .load(controlled_buffer_7_out), .clk(and_1_out), .D(rom_2_data),
    .Q(counter_3_q));  // open: up, count, carry
  ROM #(.addrWidth(4), .dataWidth(12)) rom_3 (
    .addr(counter_3_q),
    .data({out_14, out_15, out_16, out_17, out_18, out_19, out_20, out_21, out_22, out_23, out_24, out_25}));
  Counter #(.max('hffff), .width(16)) counter_4 (
    .clk(and_1_out), .carry(counter_4_carry), .Q(out_12));  // open: clr, load, up, count, D

  assign out_26 = {out_14, out_15, out_16, out_17, out_18, out_19, out_20, out_21, out_22, out_23, out_24, out_25};

  // Notes on the sheet:
  //   in_1: initial=0x1
  //   Cp
  //   Ep
  //   Lm^
  //   CpEpLm.CE. 
  //   La^
  //   Ea
  //   Su
  //   CE^
  //   Li^
  //   Ei^
  //   Li.Ei.La.Ea
  //   Eu
  //   Lb^
  //   Lo^
  //   SuEuLb.Lo.
  //   contents of rom_1 (hex, n*v repeats v):
  //   3e3
  //   contents of rom_2 (hex, n*v repeats v):
  //   3 6 9 11*0 c
  //   Instruction Bits
  //   contents of rom_3 (hex, n*v repeats v):
  //   5e3 be3 263 1a3 2c3 3e3 1a3 2e1 3c7 1a3 2e1 3cf 3f2 3e3 3e3 3e3
endmodule
