// Logisim project sap_1_ttl.circ as structural Verilog: 1 circuit, main circuit main
module main (
  input  [3:0] in_1,
  input  [3:0] in_2,
  input  in_3,
  input  in_4,
  input  in_5,
  input  in_6,
  input  in_7,
  input  in_8,
  output out_9,
  output out_10,
  output out_11,
  output out_12,
  output out_13,
  output out_14,
  output out_15,
  output out_16,
  output [3:0] out_17,
  output [7:0] out_18,
  output [7:0] out_19,
  output out_20,
  output out_21,
  output out_22,
  output out_23,
  output out_24,
  output out_25,
  output out_26,
  output out_27,
  output out_28,
  output out_29,
  output out_30,
  output out_31,
  output [11:0] out_32
);

  wire and_1_out, and_4_out, and_5_out, clock_1_out, controlled_buffer_6_out, controlled_buffer_7_out,
       n74175_2_pin9, not_1_out, not_2_out, not_3_out, not_4_out, not_5_out, not_6_out, not_7_out, not_8_out;
  wire [2:0] counter_2_q;
  wire [3:0] counter_1_q, counter_3_q, n74175_1_pin2, rom_1_data;
  wire [7:0] adder_1_out, and_2_out, and_3_out, n74175_2_pin2, or_1_out, register_1_q, register_2_q;

  Clock clock_1 (.out(clock_1_out));
  and and_1 (and_1_out, not_1_out, clock_1_out);
  RAM #(.addrWidth(4), .trigger("falling"), .\type ("nonvolatile")) ram_1 (
    .addr(n74175_1_pin2), .oe(in_3), .clk(clock_1_out), .dout(out_18));  // open: we, din
  not not_1 (not_1_out, out_22);
  not not_2 (not_2_out, out_23);
  not not_3 (not_3_out, out_24);
  not not_4 (not_4_out, out_25);
  Counter #(.max('hf), .width(4)) counter_1 (
    .count(out_20), .clk(clock_1_out), .Q(counter_1_q));  // open: clr, load, up, D, carry
  _74175 u_74175_1 (
    .pin2(n74175_1_pin2[0]), .pin4(out_16), .pin5(out_15), .pin7(n74175_1_pin2[1]), .pin15(n74175_1_pin2[3]),
    .pin13(out_13), .pin12(out_14), .pin10(n74175_1_pin2[2]), .pin9(and_1_out));  // open: pin1, pin3, pin6, pin14, pin11
  Register register_1 (
    .D({out_9, out_10, out_11, out_12, out_13, out_14, out_15, out_16}), .en(not_3_out), .clk(clock_1_out),
    .Q(register_1_q));  // open: clr
  assign {out_9, out_10, out_11, out_12, out_13, out_14, out_15, out_16} = not_4_out ? register_1_q : 8'bz;  // Controlled_Buffer controlled_buffer_1
  assign {out_13, out_14, out_15, out_16} = out_21 ? counter_1_q : 4'bz;  // Controlled_Buffer controlled_buffer_2
  assign {out_9, out_10, out_11, out_12, out_13, out_14, out_15, out_16} = not_2_out ? out_18 : 8'bz;  // Controlled_Buffer controlled_buffer_3
  assign {out_9, out_10, out_11, out_12, out_13, out_14, out_15, out_16} = out_27 ? n74175_2_pin2 : 8'bz;  // Controlled_Buffer controlled_buffer_4
  assign {out_9, out_10, out_11, out_12, out_13, out_14, out_15, out_16} = out_29 ? adder_1_out : 8'bz;  // Controlled_Buffer controlled_buffer_5
  Register register_2 (
    .D({out_9, out_10, out_11, out_12, out_13, out_14, out_15, out_16}), .en(not_8_out), .clk(clock_1_out),
    .Q(register_2_q));  // open: clr
  Register register_3 (
    .D({out_9, out_10, out_11, out_12, out_13, out_14, out_15, out_16}), .en(not_7_out), .clk(clock_1_out),
    .Q(out_19));  // open: clr
  _74175 u_74175_2 (
    .pin2(n74175_2_pin2[0]), .pin4(out_16), .pin5(out_15), .pin7(n74175_2_pin2[1]), .pin15(n74175_2_pin2[3]),
    .pin13(out_13), .pin12(out_14), .pin10(n74175_2_pin2[2]), .pin9(n74175_2_pin9));  // open: pin1, pin3, pin6, pin14, pin11
  Adder adder_1 (.a(n74175_2_pin2), .b(or_1_out), .out(adder_1_out), .cin(out_28));  // open: cout
  assign or_1_out = and_2_out | and_3_out;  // OR_Gate or_1, 8 bits wide
  assign and_2_out = register_2_q & ~{8{out_28}};  // AND_Gate and_2, 8 bits wide
  assign and_3_out = ~register_2_q & {8{out_28}};  // AND_Gate and_3, 8 bits wide
  Hex_Digit_Display hex_digit_display_1 (.value(out_19[7:4]));  // open: dp
  ROM #(.addrWidth(4), .dataWidth(4)) rom_1 (.addr(register_1_q[7:4]), .data(rom_1_data));
  Counter #(.max('h5), .width(3)) counter_2 (
    .clk(clock_1_out), .Q(counter_2_q));  // open: clr, load, up, count, D, carry
  _74175 u_74175_3 (
    .pin2(n74175_2_pin2[4]), .pin4(out_12), .pin5(out_11), .pin7(n74175_2_pin2[5]), .pin15(n74175_2_pin2[7]),
    .pin13(out_9), .pin12(out_10), .pin10(n74175_2_pin2[6]), .pin9(n74175_2_pin9));  // open: pin1, pin3, pin6, pin14, pin11
  Hex_Digit_Display hex_digit_display_2 (.value(out_19[3:0]));  // open: dp
  not not_5 (not_5_out, counter_2_q[2]);
  and and_4 (and_4_out, counter_2_q[0], counter_2_q[1], not_5_out);
  and and_5 (and_5_out, ~counter_2_q[0], ~counter_2_q[1], ~counter_2_q[2]);  // AND_Gate
  assign controlled_buffer_6_out = clock_1_out ? and_5_out : 1'bz;  // Controlled_Buffer controlled_buffer_6
  not not_6 (not_6_out, out_26);
  not not_7 (not_7_out, out_31);
  assign controlled_buffer_7_out = clock_1_out ? and_4_out : 1'bz;  // Controlled_Buffer controlled_buffer_7
  and and_6 (n74175_2_pin9, not_6_out, clock_1_out);
  not not_8 (not_8_out, out_30);
  Counter #(.max('hf), .trigger("falling"), .width(4)) counter_3 (
    .clr(controlled_buffer_6_out), .load(controlled_buffer_7_out), .clk(clock_1_out), .D(rom_1_data),
    .Q(counter_3_q));  // open: up, count, carry
  ROM #(.addrWidth(4), .dataWidth(12)) rom_2 (
    .addr(counter_3_q),
    .data({out_20, out_21, out_22, out_23, out_24, out_25, out_26, out_27, out_28, out_29, out_30, out_31}));
  // _74181 74181_1: pin names not known; wires that end beside it: in_1[0], in_2[1], in_2[0], in_1[1], in_4, in_2[2], in_5, in_1[2], in_6, in_2[3], in_7, in_1[3], in_8, out_17[0], out_17[1], out_17[2], out_17[3]

  assign out_32 = {out_20, out_21, out_22, out_23, out_24, out_25, out_26, out_27, out_28, out_29, out_30, out_31};

  // Notes on the sheet:
  //   in_3: initial=0x1
  //   Cp
  //   Ep
  //   Lm^
  //   CpEpLm.CE. 
  //   La^
  //   Ea
  //   Su
  //   CE^
  //   Li^
  //   Ei^
  //   Li.Ei.La.Ea
  //   Eu
  //   Lb^
  //   Lo^
  //   SuEuLb.Lo.
  //   contents of rom_1 (hex, n*v repeats v):
  //   3 6 9 11*0 c
  //   Instruction Bits
  //   contents of rom_2 (hex, n*v repeats v):
  //   5e3 be3 263 1a3 2c3 3e3 1a3 2e1 3c7 1a3 2e1 3cf 3f2 3e3 3e3
endmodule
