// Logisim project shift_registers.circ as structural Verilog: 1 circuit, main circuit main
module main (
  input  in_1,
  input  in_2,
  input  in_3,
  input  in_4,
  input  in_5,
  input  in_6,
  input  in_7,
  input  in_8,
  input  in_9,
  input  in_10,
  input  in_11,
  input  in_12,
  input  in_13,
  input  in_14,
  input  in_15,
  input  in_16,
  input  in_17,
  input  in_18,
  output out_19,
  output out_20,
  output out_21
);

  wire and_1_out, and_2_out, and_3_out, and_4_out, and_5_out, and_6_out, and_7_out, and_8_out, and_9_out,
       and_10_out, and_11_out, and_12_out, d_ff_1_q, d_ff_3_q, d_ff_5_q, d_ff_7_q, d_ff_8_q, nor_1_out,
       or_1_out, or_2_out, or_3_out, or_4_out;

  and and_1 (and_1_out, in_3, in_9);
  and and_2 (and_2_out, d_ff_1_q, nor_1_out);
  D_Flip_Flop d_ff_1 (.D(or_1_out), .clk(in_18), .Q(d_ff_1_q));  // open: Qn, preset, reset
  LED led_1 (.in(d_ff_1_q));
  and and_3 (and_3_out, in_11, d_ff_3_q);
  or or_1 (or_1_out, and_2_out, and_1_out, and_3_out);
  D_Flip_Flop d_ff_2 (.D(in_1), .clk(in_2), .Q(out_19));  // open: Qn, preset, reset
  and and_4 (and_4_out, d_ff_3_q, nor_1_out);
  and and_5 (and_5_out, in_11, d_ff_5_q);
  or or_2 (or_2_out, and_4_out, and_6_out, and_5_out);
  D_Flip_Flop d_ff_3 (.D(or_2_out), .clk(in_18), .Q(d_ff_3_q));  // open: Qn, preset, reset
  LED led_2 (.in(d_ff_3_q));
  D_Flip_Flop d_ff_4 (.D(out_19), .clk(in_2), .Q(out_20));  // open: Qn, preset, reset
  and and_6 (and_6_out, in_4, in_9);
  LED led_3 (.in(d_ff_5_q));
  and and_7 (and_7_out, d_ff_5_q, nor_1_out);
  or or_3 (or_3_out, and_7_out, and_9_out, and_8_out);
  D_Flip_Flop d_ff_5 (.D(or_3_out), .clk(in_18), .Q(d_ff_5_q));  // open: Qn, preset, reset
  D_Flip_Flop d_ff_6 (.D(out_20), .clk(in_2), .Q(out_21));  // open: Qn, preset, reset
  and and_8 (and_8_out, in_11, d_ff_8_q);
  and and_9 (and_9_out, in_5, in_9);
  D_Flip_Flop d_ff_7 (.D(out_21), .clk(in_2), .Q(d_ff_7_q));  // open: Qn, preset, reset
  nor nor_1 (nor_1_out, in_9, in_11);
  and and_10 (and_10_out, d_ff_8_q, nor_1_out);
  or or_4 (or_4_out, and_10_out, and_11_out, and_12_out);
  D_Flip_Flop d_ff_8 (.D(or_4_out), .clk(in_18), .Q(d_ff_8_q));  // open: Qn, preset, reset
  LED led_4 (.in(d_ff_8_q));
  and and_11 (and_11_out, in_11, in_14);
  and and_12 (and_12_out, in_6, in_9);
  // Shift_Register #(.length(4)) shift_register_1: pin names not known; wires that end beside it: d_ff_7_q, in_7, in_8, in_10, in_12, in_13, in_15, in_16, in_17

  // Notes on the sheet:
  //   simple shift register
  //   controlled parallel + serial load register
  //   Load
  //   SHL
endmodule
