// Logisim project sr_latches.circ as structural Verilog: 1 circuit, main circuit main
module main (
  input  in_1,
  input  in_2,
  input  in_3,
  input  in_4,
  input  in_5,
  input  in_6,
  input  in_7,
  input  in_8,
  input  in_9,
  input  in_10,
  input  in_11,
  input  in_12,
  input  in_13,
  input  in_14,
  input  in_15,
  output out_16,
  output out_17,
  output out_18,
  output out_19,
  output out_20,
  output out_21,
  output out_22,
  output out_23,
  output Q,
  output Q_prime
);

  wire and_1_out, and_2_out, and_3_out, and_4_out, and_5_out, and_6_out, clock_1_out, clock_2_out, not_1_out,
       not_2_out, not_3_out;

  not not_1 (not_1_out, in_3);
  and and_1 (and_1_out, in_2, not_1_out);
  and and_2 (and_2_out, out_17, not_1_out);
  or or_1 (out_17, and_1_out, and_2_out);
  Clock clock_1 (.out(clock_1_out));
  not not_2 (not_2_out, in_15);
  Clock clock_2 (.out(clock_2_out));
  not not_3 (not_3_out, in_10);
  and and_3 (and_3_out, in_1, clock_1_out);
  and and_4 (and_4_out, clock_1_out, in_4);
  and and_5 (and_5_out, not_2_out, clock_2_out);
  and and_6 (and_6_out, clock_2_out, in_15);
  and and_7 (out_16, ~and_3_out, ~out_18);  // AND_Gate
  and and_8 (out_18, ~out_16, ~and_4_out);  // AND_Gate
  and and_9 (out_19, ~not_3_out, ~out_22);  // AND_Gate
  and and_10 (out_22, ~out_19, ~in_10);  // AND_Gate
  and and_11 (Q, ~and_5_out, ~Q_prime);  // AND_Gate
  and and_12 (Q_prime, ~Q, ~and_6_out);  // AND_Gate
  D_Flip_Flop d_ff_1 (.D(in_12), .clk(in_13), .Q(out_23), .preset(in_9), .reset(in_14));  // open: Qn
  J_K_Flip_Flop j_k_ff_1 (.J(in_6), .K(in_7), .clk(in_8), .Q(out_20), .Qn(out_21), .preset(in_5), .reset(in_11));

  // Notes on the sheet:
  //   set
  //   D
  //   set
  //   SR-LATCH
  //   UnClocked D-Latch
  //   Clocked DLatch
endmodule
