// Logisim project three_state_switch.circ as structural Verilog: 1 circuit, main circuit main
module main (
  input  Din,
  input  in_2,
  input  in_3,
  input  in_4,
  output Dout,
  output out_6
);

  assign Dout = in_2 ? Din : 1'bz;  // Controlled_Buffer controlled_buffer_1
  assign out_6 = in_4 ? ~in_3 : 1'bz;  // Controlled_Inverter controlled_inverter_1

  // Notes on the sheet:
  //   3-state switch
  //   ENABLE
  //   controlled inverter
endmodule
