// Logisim project transistors_invertors.circ as structural Verilog: 1 circuit, main circuit main
module main (
  input  in_1,
  input  in_2,
  input  in_3,
  input  in_4,
  output out_5
);

  wire transistor_2_out;

  Transistor #(.\type ("n")) transistor_1 (.in(in_2), .out(out_5), .gate(in_1));
  Transistor transistor_2 (.in(in_4), .out(transistor_2_out), .gate(in_3));
  LED led_1 (.in(transistor_2_out));
  // also tied to VCC on the sheet: out_5
endmodule
