// Logisim project sap2.circ as structural Verilog
module main (
  input  in_1,
  input  in_2,
  input  in_3,
  input  [1:0] in_4,
  output out_5,
  output out_6,
  output out_7,
  output out_8,
  output out_9,
  output out_10,
  output out_11,
  output out_12,
  output out_13,
  output [7:0] out_14,
  output [15:0] out_15,
  output [7:0] out_16,
  output out_17,
  output out_18,
  output out_19,
  output out_20,
  output out_21,
  output out_22,
  output out_23,
  output out_24,
  output out_25,
  output out_26,
  output out_27,
  output out_28,
  output [11:0] out_29
);

  wire and_1_out, and_4_out, and_5_out, clock_1_out, comparator_1_eq, controlled_buffer_6_out,
       controlled_buffer_7_out, counter_1_carry, counter_4_carry, not_1_out, not_2_out, not_3_out, not_4_out,
       not_5_out, not_6_out, not_7_out, not_8_out;
  wire [2:0] counter_2_q;
  wire [3:0] counter_1_q, counter_3_q, register_1_q, rom_2_data;
  wire [7:0] adder_1_out, and_2_out, and_3_out, or_1_out, register_2_q, register_3_q, register_4_q;
  wire [11:0] rom_1_data;

  Clock clock_1 (.out(clock_1_out));
  and and_1 (and_1_out, ~counter_1_carry, clock_1_out);  // AND_Gate
  not not_1 (not_1_out, out_19);
  not not_2 (not_2_out, out_20);
  not not_3 (not_3_out, out_21);
  Counter #(.max('hf), .width(4)) counter_1 (
    .count(out_17), .clk(and_1_out), .carry(counter_1_carry), .Q(counter_1_q));  // open: clr, load, up, D
  RAM #(.addrWidth(4), .trigger("falling"), .\type ("nonvolatile")) ram_1 (
    .addr(register_1_q), .oe(in_3), .clk(and_1_out), .dout(out_14));  // open: we, din
  not not_4 (not_4_out, out_22);
  Register #(.width(4)) register_1 (
    .D({out_9, out_10, out_11, out_12}), .en(not_1_out), .clk(and_1_out), .Q(register_1_q));  // open: clr
  Register register_2 (
    .D({out_5, out_6, out_7, out_8, out_9, out_10, out_11, out_12}), .en(not_3_out), .clk(and_1_out),
    .Q(register_2_q));  // open: clr
  assign {out_9, out_10, out_11, out_12} = out_18 ? counter_1_q : 4'bz;  // Controlled_Buffer controlled_buffer_1
  assign {out_5, out_6, out_7, out_8, out_9, out_10, out_11, out_12} = not_4_out ? register_2_q : 8'bz;  // Controlled_Buffer controlled_buffer_2
  assign {out_5, out_6, out_7, out_8, out_9, out_10, out_11, out_12} = not_2_out ? out_14 : 8'bz;  // Controlled_Buffer controlled_buffer_3
  ROM #(.addrWidth(2), .dataWidth(12)) rom_1 (.addr(in_4), .data(rom_1_data));
  assign {out_5, out_6, out_7, out_8, out_9, out_10, out_11, out_12} = out_24 ? register_3_q : 8'bz;  // Controlled_Buffer controlled_buffer_4
  assign {out_5, out_6, out_7, out_8, out_9, out_10, out_11, out_12} = out_26 ? adder_1_out : 8'bz;  // Controlled_Buffer controlled_buffer_5
  Register register_3 (
    .D({out_5, out_6, out_7, out_8, out_9, out_10, out_11, out_12}), .en(not_7_out), .clk(and_1_out),
    .Q(register_3_q));  // open: clr
  assign or_1_out = and_2_out | and_3_out;  // OR_Gate or_1, 8 bits wide
  assign and_2_out = register_4_q & ~{8{out_25}};  // AND_Gate and_2, 8 bits wide
  Register register_4 (
    .D({out_5, out_6, out_7, out_8, out_9, out_10, out_11, out_12}), .en(not_8_out), .clk(and_1_out),
    .Q(register_4_q));  // open: clr
  Register register_5 (
    .D({out_5, out_6, out_7, out_8, out_9, out_10, out_11, out_12}), .en(not_6_out), .clk(and_1_out),
    .Q(out_16));  // open: clr
  Adder adder_1 (.a(register_3_q), .b(or_1_out), .out(adder_1_out), .cin(out_25));  // open: cout
  assign and_3_out = ~register_4_q & {8{out_25}};  // AND_Gate and_3, 8 bits wide
  ROM #(.addrWidth(4), .dataWidth(4)) rom_2 (.addr(register_2_q[7:4]), .data(rom_2_data));
  Hex_Digit_Display hex_digit_display_1 (.value(out_16[7:4]));  // open: dp
  Hex_Digit_Display hex_digit_display_2 (.value(out_16[3:0]));  // open: dp
  Counter #(.max('h5), .width(3)) counter_2 (.clk(and_1_out), .Q(counter_2_q));  // open: clr, load, up, count, D, carry
  not not_5 (not_5_out, counter_2_q[2]);
  and and_4 (and_4_out, ~counter_2_q[0], ~counter_2_q[1], ~counter_2_q[2]);  // AND_Gate
  Comparator #(.width(12)) comparator_1 (
    .a(rom_1_data),
    .b({out_17, out_18, out_19, out_20, out_21, out_22, out_23, out_24, out_25, out_26, out_27, out_28}),
    .eq(comparator_1_eq));  // open: gt, lt
  not not_6 (not_6_out, out_28);
  and and_5 (and_5_out, counter_2_q[0], counter_2_q[1], not_5_out);
  assign controlled_buffer_6_out = and_1_out ? and_4_out : 1'bz;  // Controlled_Buffer controlled_buffer_6
  not not_7 (not_7_out, out_23);
  Counter #(.max('hf), .trigger("falling"), .width(4)) counter_3 (
    .clr(controlled_buffer_6_out), .load(controlled_buffer_7_out), .clk(and_1_out), .D(rom_2_data),
    .Q(counter_3_q));  // open: up, count, carry
  assign controlled_buffer_7_out = and_1_out ? and_5_out : 1'bz;  // Controlled_Buffer controlled_buffer_7
  ROM #(.addrWidth(4), .dataWidth(12)) rom_3 (
    .addr(counter_3_q),
    .data({out_17, out_18, out_19, out_20, out_21, out_22, out_23, out_24, out_25, out_26, out_27, out_28}));
  not not_8 (not_8_out, out_27);
  RAM #(.addrWidth(16)) ram_2 ();  // open: addr, we, oe, clk, din, dout
  Counter #(.max('hffff), .width(16)) counter_4 (
    .clk(and_1_out), .carry(counter_4_carry), .Q(out_15));  // open: clr, load, up, count, D
  dummy dummy_1 (.in_1(in_1), .in_2(in_2), .out_3(out_13));

  assign out_29 = {out_17, out_18, out_19, out_20, out_21, out_22, out_23, out_24, out_25, out_26, out_27, out_28};

  // Notes on the sheet:
  //   in_3: initial=0x1
  //   Cp
  //   Ep
  //   Lm^
  //   CE^
  //   Li^
  //   Ei^
  //   CpEpLm.CE. 
  //   Eu
  //   Lb^
  //   Lo^
  //   La^
  //   Ea
  //   Su
  //   Li.Ei.La.Ea
  //   SuEuLb.Lo.
  //   contents of rom_1 (hex, n*v repeats v):
  //   3e3
  //   contents of rom_2 (hex, n*v repeats v):
  //   3 6 9 11*0 c
  //   Instruction Bits
  //   contents of rom_3 (hex, n*v repeats v):
  //   5e3 be3 263 1a3 2c3 3e3 1a3 2e1 3c7 1a3 2e1 3cf 3f2 3e3 3e3 3e3
endmodule

module dummy (
  input  in_1,
  input  in_2,
  output out_3
);

  Clock clock_1 (.out(in_2));
  and and_1 (out_3, in_1, in_2);
endmodule

module program_counter_16b (
  input  in_1,
  input  in_2,
  input  in_3,
  input  in_4,
  input  [15:0] load_input,
  input  in_6,
  output out_7,
  output [15:0] out_8
);

  wire [15:0] counter_1_q;

  Counter #(.max('hffff), .width(16)) counter_1 (
    .clr(in_1), .load(in_3), .count(in_2), .clk(in_4), .D(load_input), .carry(out_7), .Q(counter_1_q));  // open: up
  assign out_8 = in_6 ? counter_1_q : 16'bz;  // Controlled_Buffer controlled_buffer_1
endmodule

module sap_2 (
  input  serial_in,
  input  in_2,
  output [7:0] A,
  output [7:0] out_4,
  output [7:0] regA,
  output [7:0] A_hex,
  output [7:0] regB,
  output [7:0] out_8,
  output [7:0] regC,
  output [7:0] out_10,
  output [7:0] out_11,
  output [7:0] out_12,
  output [7:0] out_13,
  output [7:0] out_14
);

  wire alu_8b_1_negative_flag, alu_8b_1_zero_flag, and_1_out, and_2_out, and_3_out, and_4_out, and_5_out,
       and_6_out, clock_1_out, d_ff_1_q, demultiplexer_1_out1, demultiplexer_1_out2, flags_1_out_5,
       flags_1_out_6, inputport1_1_read_enable, inputport1_1_ready, keyboard_1_avail, or_1_out, or_2_out,
       or_3_out, or_4_out, outputport4_1_acknowledge_flag;
  wire [1:0] program_counter_out_8_2, register_1_q;
  wire [3:0] outputport3_1_nibble0, outputport3_1_nibble1;
  wire [6:0] keyboard_1_data;
  wire [7:0] accumulator_out_6, alu_8b_1_out_4, B_out_6, bit_expander_16_8_1_out_3,
       bit_expander_16_8_3_out_3, bit_expander_16_8_4_out_3, bit_expander_16_8_5_out_3,
       bit_expander_16_8_6_out_3, bit_expander_16_8_7_out_3, bit_expander_16_8_8_out_3, C_out_6,
       controlled_buffer_1_out, controlled_buffer_2_out, inputport2_1_status_byte,
       instruction_register_out_6, memory_data_register_out_6, ram_1_dout, tmp_out_6;
  wire [15:0] bus_filter_1_out_5, bus_filter_2_out_5, controlled_buffer_3_out, controlled_buffer_6_out,
       ref_out_7, register_16b_1_out_6, register_16b_1_out_7;
  wire [15:2] program_counter_out_8;
  wire [63:0] controller_sequencer_1_out_5;

  D_Flip_Flop d_ff_1 (.D(controller_sequencer_1_out_5[41]), .clk(and_1_out), .Q(d_ff_1_q));  // open: Qn, preset, reset
  Clock clock_1 (.out(clock_1_out));
  and and_1 (and_1_out, clock_1_out, ~d_ff_1_q);  // AND_Gate
  and and_2 (and_2_out, controller_sequencer_1_out_5[40], and_1_out);
  RAM #(.addrWidth(16), .enables("line"), .\type ("nonvolatile")) ram_1 (
    .addr(register_16b_1_out_6), .we(controller_sequencer_1_out_5[7]), .clk(and_1_out),
    .din(controlled_buffer_2_out), .dout(ram_1_dout));
  assign controlled_buffer_1_out = controller_sequencer_1_out_5[11] ? ram_1_dout : 8'bz;  // Controlled_Buffer controlled_buffer_1
  assign controlled_buffer_2_out = controller_sequencer_1_out_5[13] ? memory_data_register_out_6 : 8'bz;  // Controlled_Buffer controlled_buffer_2
  register_16b register_16b_1 (
    .in_1(controller_sequencer_1_out_5[5]), .in_2(controlled_buffer_3_out), .in_3(or_1_out),
    .in_4(and_1_out), .in_5(controller_sequencer_1_out_5[6]), .out_6(register_16b_1_out_6),
    .out_7(register_16b_1_out_7));
  register_8b memory_data_register (
    .in_1(controller_sequencer_1_out_5[9]), .in_2(controlled_buffer_1_out),
    .in_3(controller_sequencer_1_out_5[8]), .in_4(and_1_out), .out_6(memory_data_register_out_6));  // open: in_5, out_7
  and and_3 (and_3_out, flags_1_out_6, controller_sequencer_1_out_5[45]);
  and and_4 (and_4_out, ~flags_1_out_6, controller_sequencer_1_out_5[46]);  // AND_Gate
  and and_5 (and_5_out, flags_1_out_5, controller_sequencer_1_out_5[47]);
  and and_6 (and_6_out, ~flags_1_out_5, controller_sequencer_1_out_5[48]);  // AND_Gate
  or or_1 (or_1_out, controller_sequencer_1_out_5[4], or_3_out);
  program_counter_16b program_counter (
    .in_1(controller_sequencer_1_out_5[1]), .in_3(controller_sequencer_1_out_5[2]),
    .load_input({program_counter_out_8, program_counter_out_8_2}), .in_6(controller_sequencer_1_out_5[3]),
    .in_4(and_1_out), .in_2(controller_sequencer_1_out_5[0]),
    .out_8({program_counter_out_8, program_counter_out_8_2}));  // open: out_7
  assign controlled_buffer_3_out = controller_sequencer_1_out_5[4] ? {program_counter_out_8, program_counter_out_8_2} : 16'bz;  // Controlled_Buffer controlled_buffer_3
  bit_expander_8_by_16 bit_expander_8_by_16_1 (
    .in_2(memory_data_register_out_6), .in_1(controller_sequencer_1_out_5[12]),
    .out_3({program_counter_out_8, program_counter_out_8_2}));
  bit_expander_16_8 bit_expander_16_8_1 (
    .in_2({program_counter_out_8, program_counter_out_8_2}), .in_1(controller_sequencer_1_out_5[37]),
    .out_3(bit_expander_16_8_1_out_3));
  bus_filter bus_filter_1 (
    .in_3({program_counter_out_8, program_counter_out_8_2}), .current_mar_value(register_16b_1_out_7),
    .Hw(controller_sequencer_1_out_5[43]), .Lw(controller_sequencer_1_out_5[42]), .out_5(bus_filter_1_out_5));
  bit_expander_16_8 bit_expander_16_8_2 (
    .in_2({program_counter_out_8, program_counter_out_8_2}), .in_1(controller_sequencer_1_out_5[10]),
    .out_3(controlled_buffer_1_out));
  register_8b instruction_register (
    .in_1(1'b1), .in_2(bit_expander_16_8_1_out_3), .in_3(controller_sequencer_1_out_5[37]), .in_4(and_1_out),
    .in_5(controller_sequencer_1_out_5[39]), .out_6(instruction_register_out_6));  // open: out_7
  controller_sequencer controller_sequencer_1 (
    .in_3(or_2_out), .clk(and_1_out), .controller_in(instruction_register_out_6),
    .out_5(controller_sequencer_1_out_5), .out_4(out_13));
  or or_2 (or_2_out, and_2_out, and_3_out, and_6_out, and_4_out, and_5_out);
  assign controlled_buffer_3_out = or_3_out ? bus_filter_1_out_5 : 16'bz;  // Controlled_Buffer controlled_buffer_4
  assign {program_counter_out_8, program_counter_out_8_2} = controller_sequencer_1_out_5[44] ? register_16b_1_out_7 : 16'bz;  // Controlled_Buffer controlled_buffer_5
  bit_expander_16_8 bit_expander_16_8_3 (
    .in_2({program_counter_out_8, program_counter_out_8_2}), .in_1(controller_sequencer_1_out_5[25]),
    .out_3(bit_expander_16_8_3_out_3));
  or or_3 (or_3_out, controller_sequencer_1_out_5[43], controller_sequencer_1_out_5[42]);
  bit_expander_16_8 bit_expander_16_8_4 (
    .in_2({program_counter_out_8, program_counter_out_8_2}), .in_1(controller_sequencer_1_out_5[28]),
    .out_3(bit_expander_16_8_4_out_3));
  bit_expander_16_8 bit_expander_16_8_5 (
    .in_2({program_counter_out_8, program_counter_out_8_2}), .in_1(controller_sequencer_1_out_5[31]),
    .out_3(bit_expander_16_8_5_out_3));
  bit_expander_16_8 bit_expander_16_8_6 (
    .in_2({program_counter_out_8, program_counter_out_8_2}), .in_1(controller_sequencer_1_out_5[34]),
    .out_3(bit_expander_16_8_6_out_3));
  assign controlled_buffer_6_out = controller_sequencer_1_out_5[50] ? {program_counter_out_8, program_counter_out_8_2} : 16'bz;  // Controlled_Buffer controlled_buffer_6
  register_8b accumulator (
    .in_1(controller_sequencer_1_out_5[26]), .in_2(bit_expander_16_8_3_out_3),
    .in_3(controller_sequencer_1_out_5[25]), .in_4(and_1_out), .in_5(controller_sequencer_1_out_5[27]),
    .out_6(accumulator_out_6), .out_7(A));
  alu_8b alu_8b_1 (
    .Acc(A), .Tmp(out_4), .alu_op(controller_sequencer_1_out_5[23:14]),
    .negative_flag(alu_8b_1_negative_flag), .zero_flag(alu_8b_1_zero_flag), .out_4(alu_8b_1_out_4));
  register_8b tmp (
    .in_1(controller_sequencer_1_out_5[29]), .in_2(bit_expander_16_8_4_out_3),
    .in_3(controller_sequencer_1_out_5[28]), .in_4(and_1_out), .in_5(controller_sequencer_1_out_5[30]),
    .out_6(tmp_out_6), .out_7(out_4));
  register_8b B (
    .in_1(controller_sequencer_1_out_5[32]), .in_2(bit_expander_16_8_5_out_3),
    .in_3(controller_sequencer_1_out_5[31]), .in_4(and_1_out), .in_5(controller_sequencer_1_out_5[33]),
    .out_6(B_out_6), .out_7(out_10));
  register_8b C (
    .in_1(controller_sequencer_1_out_5[35]), .in_2(bit_expander_16_8_6_out_3),
    .in_3(controller_sequencer_1_out_5[34]), .in_4(and_1_out), .in_5(controller_sequencer_1_out_5[36]),
    .out_6(C_out_6), .out_7(out_11));
  assign controlled_buffer_6_out = or_4_out ? bus_filter_2_out_5 : 16'bz;  // Controlled_Buffer controlled_buffer_7
  or or_4 (or_4_out, controller_sequencer_1_out_5[52], controller_sequencer_1_out_5[51]);
  register_16b \ref  (
    .in_1(controller_sequencer_1_out_5[49]), .in_2(controlled_buffer_6_out),
    .in_3(controller_sequencer_1_out_5[50]), .in_4(and_1_out),
    .out_6({program_counter_out_8, program_counter_out_8_2}), .out_7(ref_out_7));  // open: in_5
  bus_filter bus_filter_2 (
    .in_3({program_counter_out_8, program_counter_out_8_2}), .current_mar_value(ref_out_7),
    .Hw(controller_sequencer_1_out_5[52]), .Lw(controller_sequencer_1_out_5[51]), .out_5(bus_filter_2_out_5));
  bit_expander_8_by_16 bit_expander_8_by_16_2 (
    .in_2(accumulator_out_6), .in_1(controller_sequencer_1_out_5[26]),
    .out_3({program_counter_out_8, program_counter_out_8_2}));
  bit_expander_8_by_16 bit_expander_8_by_16_3 (
    .in_2(alu_8b_1_out_4), .in_1(controller_sequencer_1_out_5[24]),
    .out_3({program_counter_out_8, program_counter_out_8_2}));
  bit_expander_8_by_16 bit_expander_8_by_16_4 (
    .in_2(tmp_out_6), .in_1(controller_sequencer_1_out_5[29]),
    .out_3({program_counter_out_8, program_counter_out_8_2}));
  bit_expander_8_by_16 bit_expander_8_by_16_5 (
    .in_2(B_out_6), .in_1(controller_sequencer_1_out_5[32]),
    .out_3({program_counter_out_8, program_counter_out_8_2}));
  bit_expander_8_by_16 bit_expander_8_by_16_6 (
    .in_2(C_out_6), .in_1(controller_sequencer_1_out_5[35]),
    .out_3({program_counter_out_8, program_counter_out_8_2}));
  Flags flags_1 (
    .alu_op(controller_sequencer_1_out_5[23:14]), .n_flag(alu_8b_1_negative_flag),
    .z_flag(alu_8b_1_zero_flag), .clk(and_1_out), .out_5(flags_1_out_5), .out_6(flags_1_out_6));
  Hex_Digit_Display hex_digit_display_1 (.value(outputport3_1_nibble1));  // open: dp
  Hex_Digit_Display hex_digit_display_2 (.value(outputport3_1_nibble0));  // open: dp
  Keyboard #(.buflen(2)) keyboard_1 (
    .clk(and_1_out), .re(inputport1_1_read_enable), .clr(inputport1_1_ready), .avail(keyboard_1_avail),
    .data(keyboard_1_data));
  Register #(.width(2)) register_1 (
    .D(program_counter_out_8_2), .en(controller_sequencer_1_out_5[53]), .clk(and_1_out), .Q(register_1_q));  // open: clr
  InputPort1 inputport1_1 (
    .buffer_status(keyboard_1_avail), .kb_input(keyboard_1_data), .clk(and_1_out),
    .ack(controller_sequencer_1_out_5[54]), .read_enable(inputport1_1_read_enable), .port_output(out_12),
    .ready(inputport1_1_ready));
  InputPort2 inputport2_1 (.ready(inputport1_1_ready), .serial_in(serial_in), .status_byte(inputport2_1_status_byte));
  Demultiplexer #(.select(2)) demultiplexer_1 (
    .out1(demultiplexer_1_out1), .out2(demultiplexer_1_out2), .in(controller_sequencer_1_out_5[55]),
    .sel(register_1_q));  // open: out0, out3
  OutputPort3 outputport3_1 (
    .bus_in(bit_expander_16_8_7_out_3), .clk(and_1_out), .out_3_enable(controller_sequencer_1_out_5[56]),
    .nibble0(outputport3_1_nibble0), .nibble1(outputport3_1_nibble1));
  bit_expander_8_by_16 bit_expander_8_by_16_7 (
    .in_2(out_12), .in_1(demultiplexer_1_out1), .out_3({program_counter_out_8, program_counter_out_8_2}));
  bit_expander_8_by_16 bit_expander_8_by_16_8 (
    .in_2(inputport2_1_status_byte), .in_1(demultiplexer_1_out2),
    .out_3({program_counter_out_8, program_counter_out_8_2}));
  bit_expander_16_8 bit_expander_16_8_7 (
    .in_2({program_counter_out_8, program_counter_out_8_2}), .in_1(controller_sequencer_1_out_5[56]),
    .out_3(bit_expander_16_8_7_out_3));
  bit_expander_16_8 bit_expander_16_8_8 (
    .in_2({program_counter_out_8, program_counter_out_8_2}), .in_1(controller_sequencer_1_out_5[57]),
    .out_3(bit_expander_16_8_8_out_3));
  OutputPort4 outputport4_1 (
    .in_1(bit_expander_16_8_8_out_3), .clk(and_1_out), .out_4_write(controller_sequencer_1_out_5[57]),
    .ack_signal(in_2), .out_bits(out_14), .acknowledge_flag(outputport4_1_acknowledge_flag));
  LED led_1 (.in(outputport4_1_acknowledge_flag));

  assign A_hex = A;
  assign out_8 = A;
  assign regA = A;
  assign regB = out_10;
  assign regC = out_11;

  // Notes on the sheet:
  //   useless
  //   output_display
  //   kb input
endmodule

module register_16b (
  input  in_1,
  input  [15:0] in_2,
  input  in_3,
  input  in_4,
  input  in_5,
  output [15:0] out_6,
  output [15:0] out_7
);

  Register #(.width(16)) register_1 (.D(in_2), .en(in_3), .clk(in_4), .Q(out_7), .clr(in_5));
  assign out_6 = in_1 ? out_7 : 16'bz;  // Controlled_Buffer controlled_buffer_1
endmodule

module memory_64k_8b (
  input  [15:0] in_1,
  input  in_2,
  input  in_3,
  input  [7:0] in_4,
  output [7:0] out_5
);

  RAM #(.addrWidth(16), .enables("line"), .\type ("nonvolatile")) raaaa (
    .addr(in_1), .we(in_2), .clk(in_3), .din(in_4), .dout(out_5));
endmodule

module register_8b (
  input  in_1,
  input  [7:0] in_2,
  input  in_3,
  input  in_4,
  input  in_5,
  output [7:0] out_6,
  output [7:0] out_7
);

  Register register_1 (.D(in_2), .en(in_3), .clk(in_4), .Q(out_7), .clr(in_5));
  assign out_6 = in_1 ? out_7 : 8'bz;  // Controlled_Buffer controlled_buffer_1
endmodule

module alu_8b (
  input  [9:0] alu_op,
  input  [7:0] Acc,
  input  [7:0] Tmp,
  output [7:0] out_4,
  output negative_flag,
  output zero_flag
);

  wire nor_1_out, or_1_out, or_2_out, or_4_out;
  wire [7:0] and_1_out, controlled_buffer_1_out, controlled_buffer_4_out, not_1_out, not_2_out, or_3_out,
       shifter_1_out, shifter_2_out, xor_1_out;

  assign controlled_buffer_1_out = alu_op[2] ? Tmp : 8'bz;  // Controlled_Buffer controlled_buffer_1
  or or_1 (or_1_out, alu_op[0], alu_op[1]);
  assign controlled_buffer_1_out = or_1_out ? Acc : 8'bz;  // Controlled_Buffer controlled_buffer_2
  assign controlled_buffer_1_out = alu_op[3] ? 8'h1 : 8'bz;  // Controlled_Buffer controlled_buffer_3
  assign not_1_out = ~Tmp;  // NOT_Gate not_1, 8 bits wide
  assign not_2_out = ~8'h1;  // NOT_Gate not_2, 8 bits wide
  assign controlled_buffer_4_out = alu_op[1] ? not_1_out : 8'bz;  // Controlled_Buffer controlled_buffer_4
  assign controlled_buffer_4_out = alu_op[0] ? Tmp : 8'bz;  // Controlled_Buffer controlled_buffer_5
  assign controlled_buffer_4_out = alu_op[3] ? Tmp : 8'bz;  // Controlled_Buffer controlled_buffer_6
  assign controlled_buffer_4_out = alu_op[2] ? not_2_out : 8'bz;  // Controlled_Buffer controlled_buffer_7
  Shifter #(.shift("rr")) shifter_1 (.in(Tmp), .\dist (3'b001), .out(shifter_1_out));
  or or_2 (or_2_out, alu_op[2], alu_op[1]);
  Adder adder_1 (
    .a(controlled_buffer_1_out), .b(controlled_buffer_4_out), .out({negative_flag, out_4[6:0]}),
    .cin(or_2_out));  // open: cout
  assign {negative_flag, out_4[6:0]} = alu_op[7] ? shifter_2_out : 8'bz;  // Controlled_Buffer controlled_buffer_8
  Shifter #(.shift("rl")) shifter_2 (.in(Tmp), .\dist (3'b001), .out(shifter_2_out));
  assign {negative_flag, out_4[6:0]} = alu_op[8] ? shifter_1_out : 8'bz;  // Controlled_Buffer controlled_buffer_9
  assign and_1_out = Acc & Tmp;  // AND_Gate and_1, 8 bits wide
  assign xor_1_out = Acc ^ Tmp;  // XOR_Gate xor_1, 8 bits wide
  assign {negative_flag, out_4[6:0]} = alu_op[6] ? xor_1_out : 8'bz;  // Controlled_Buffer controlled_buffer_10
  assign or_3_out = Acc | Tmp;  // OR_Gate or_3, 8 bits wide
  assign {negative_flag, out_4[6:0]} = alu_op[5] ? or_3_out : 8'bz;  // Controlled_Buffer controlled_buffer_11
  assign {negative_flag, out_4[6:0]} = alu_op[4] ? and_1_out : 8'bz;  // Controlled_Buffer controlled_buffer_12
  assign {negative_flag, out_4[6:0]} = alu_op[9] ? not_1_out : 8'bz;  // Controlled_Buffer controlled_buffer_13
  or or_4 (or_4_out, alu_op[0], alu_op[1], alu_op[2], alu_op[3], alu_op[4], alu_op[5], alu_op[6], alu_op[7], alu_op[8], alu_op[9]);
  nor nor_1 (nor_1_out, negative_flag, out_4[6], out_4[5], out_4[4], out_4[3], out_4[2], out_4[1], out_4[0]);
  assign zero_flag = or_4_out ? nor_1_out : 1'bz;  // Controlled_Buffer controlled_buffer_14

  assign out_4[7] = negative_flag;

  // Notes on the sheet:
  //   dcr
  //   inr
  //   and
  //   add
  //   sub
endmodule

module bit_expander_8_by_16 (
  input  in_1,
  input  [7:0] in_2,
  output [15:0] out_3
);

  assign out_3 = in_1 ? {{8{1'b0}}, in_2} : 16'bz;  // Controlled_Buffer controlled_buffer_1
endmodule

module bit_expander_16_8 (
  input  in_1,
  input  [15:0] in_2,
  output [7:0] out_3
);

  assign out_3 = in_1 ? in_2[7:0] : 8'bz;  // Controlled_Buffer controlled_buffer_1
endmodule

module controller_sequencer (
  input  [7:0] controller_in,
  input  clk,
  input  in_3,
  output [7:0] out_4,
  output [63:0] out_5
);

  wire and_1_out, and_2_out, and_3_out;
  wire [3:0] counter_1_q;
  wire [7:0] rom_1_data;

  ROM rom_1 (.addr(controller_in), .data(rom_1_data));
  and and_1 (and_1_out, ~counter_1_q[0], ~counter_1_q[1], counter_1_q[2], ~counter_1_q[3]);  // AND_Gate
  and and_2 (and_2_out, ~counter_1_q[0], ~counter_1_q[1], ~counter_1_q[2], ~counter_1_q[3]);  // AND_Gate
  Counter #(.max('hf), .width(4)) counter_1 (
    .clr(in_3), .clk(clk), .Q(counter_1_q));  // open: load, up, count, D, carry
  Counter counter_2 (.clr(in_3), .load(and_1_out), .clk(clk), .D(rom_1_data), .Q(out_4));  // open: up, count, carry
  // OR_Gate or_1 has open pins: in0=in_3, in1=and_3_out, out=open
  and and_3 (and_3_out, counter_1_q[0], counter_1_q[1], counter_1_q[2], counter_1_q[3]);
  ROM #(.dataWidth(64)) rom_2 (.addr(out_4), .data(out_5));

  // Notes on the sheet:
  //   contents of rom_1 (hex, n*v repeats v):
  //   ff 0 0 0 63 5a 21 5*0 66 5d 26 8*0 87 7*0 8a 15*0 4a 0 0 2b 7*0 4 0 60 4d 1c 0 0 16 5*0 14 1a 6*0 18
  //   38*0 bd 0 10 12 6*0 37 3a 14*0 75 78 14*0 3d 40 6*0 7b 7e 6*0 69 6c 16*0 a4 8d 5*0 cb b0 0 0 be 5*0
  //   d4 d6 6*0 cd 10*0 43 7*0 81 7*0 6f 0 0 0 98
  //   contents of rom_2 (hex, n*v repeats v):
  //   18 21 920 2000001200 18 21 920 10001200 18 21 920 80000001200 40020000000 920 2001200 10000000000
  //   102000000 10000000000 802000000 10000000000 84000000 10000000000 880000000 10000000000 404000000
  //   10000000000 500000000 10000000000 18 21 920 2001200 10000000000 18 21 920 80001200 10000000000 18 21
  //   920 400001200 10000000000 18 21 920 10001200 18 21 920 80000001200 40020000000 4000520 22a0
  //   10000000000 110000000 3004000 10000000000 810000000 3004000 10000000000 110000000 3040000
  //   10000000000 810000000 3040000 10000000000 0 18 21 920 10001200 3040000 10000000000 14000000 3800000
  //   10000000000 14000000 3010000 10000000000 10*0 110000000 81010000 10000000000 810000000 401010000
  //   10000000000 14000000 3020000 10000000000 110000000 81020000 10000000000 810000000 401020000
  //   10000000000 110000000 3080000 10000000000 810000000 3080000 10000000000 18 21 920 10001200 3080000
  //   10000000000 110000000 3008000 10000000000 810000000 3008000 10000000000 110000000 3100000
  //   10000000000 810000000 3100000 10000000000 18 21 920 10001200 3100000 10000000000 14000000 3200000
  //   10000000000 14000000 3400000 10000000000 18 21 920 10001200 18 21 920 80000001200 40020000000
  //   100000000004 10000000000 18 21 920 10001200 18 21 1000000000000 920 80000001200 40020000000
  //   100000000004 10000000000 18 21 920 10001200 18 21 200000000000 920 80000001200 40020000000
  //   100000000004 10000000000 18 21 920 10001200 18 21 400000000000 920 80000001200 40020000000
  //   100000000004 0 10000000000 20000000000 18 21 920 10001200 18 21 920 80000001200 40020000000
  //   4000000000008 1 100000000004 10000000000 2000000000004 10000000000 18 21 920 20000000001200
  //   80000002000000 40000000000000 10000000000 100000004000000 10000000000 200000004000000 10000000000
  //   39*0 10000000000
endmodule

module Flags (
  input  [9:0] alu_op,
  input  n_flag,
  input  z_flag,
  input  clk,
  output out_5,
  output out_6
);

  wire and_1_out, and_2_out, or_1_out;

  or or_1 (or_1_out, alu_op[0], alu_op[1], alu_op[2], alu_op[3], alu_op[4], alu_op[5], alu_op[6], alu_op[7], alu_op[8], alu_op[9]);
  and and_1 (and_1_out, or_1_out, clk);
  and and_2 (and_2_out, or_1_out, clk);
  D_Flip_Flop d_ff_1 (.D(n_flag), .clk(and_1_out), .Q(out_5));  // open: Qn, preset, reset
  D_Flip_Flop d_ff_2 (.D(z_flag), .clk(and_2_out), .Q(out_6));  // open: Qn, preset, reset
endmodule

module test_ground (
  input  [15:0] in_1,
  input  in_2,
  input  in_3,
  output [7:0] out_4
);

  memory_64k_8b asdasd (.in_1(in_1), .in_2(in_2), .in_3(in_3), .out_5(out_4));  // open: in_4
  // SocVga socvga_1: pin names not known
endmodule

module bus_filter (
  input  [15:0] current_mar_value,
  input  Lw,
  input  [15:0] in_3,
  input  Hw,
  output [15:0] out_5
);

  assign out_5 = Lw ? {current_mar_value[15:8], in_3[7:0]} : 16'bz;  // Controlled_Buffer controlled_buffer_1
  assign out_5 = Hw ? {in_3[7:0], current_mar_value[7:0]} : 16'bz;  // Controlled_Buffer controlled_buffer_2
endmodule

module hex_keyboard (
  input  reset,
  output out_2,
  output ready
);

  wire and_1_out, and_2_out, and_3_out, and_4_out, clk_out;
  wire [1:0] counter_1_q;
  wire [3:0] rom_1_data;
  wire [6:0] keyboard_1_data;

  Clock clk (.out(clk_out));
  and and_1 (and_1_out, ~ready, out_2);  // AND_Gate
  Keyboard #(.buflen(2)) keyboard_1 (.clk(clk_out), .re(and_1_out), .clr(reset), .avail(out_2), .data(keyboard_1_data));
  Counter #(.max('h2), .width(2)) counter_1 (
    .clr(reset), .count(and_1_out), .clk(clk_out), .Q(counter_1_q));  // open: load, up, D, carry
  and and_2 (and_2_out, ~counter_1_q[0], ~counter_1_q[1]);  // AND_Gate
  and and_3 (and_3_out, counter_1_q[0], ~counter_1_q[1]);  // AND_Gate
  and and_4 (and_4_out, ~counter_1_q[0], counter_1_q[1]);  // AND_Gate
  ROM #(.addrWidth(7), .dataWidth(4)) rom_1 (.addr(keyboard_1_data), .data(rom_1_data));
  Register #(.width(4)) register_1 (.D(rom_1_data), .en(and_2_out), .clk(clk_out), .clr(reset));  // open: Q
  Register #(.width(4)) register_2 (.D(rom_1_data), .en(and_3_out), .clk(clk_out), .clr(reset));  // open: Q
  D_Flip_Flop d_ff_1 (.D(and_4_out), .clk(and_4_out), .Q(ready), .reset(reset));  // open: Qn, preset

  // Notes on the sheet:
  //   contents of rom_1 (hex, n*v repeats v):
  //   49*0 1 2 3 4 5 6 7 8 9 39*0 a b c d e f
endmodule

module InputPort1 (
  input  buffer_status,
  input  [6:0] kb_input,
  input  clk,
  input  ack,
  output read_enable,
  output [7:0] port_output,
  output ready
);

  wire and_2_out, and_3_out, and_4_out;
  wire [1:0] counter_1_q;
  wire [3:0] rom_1_data;

  and and_1 (read_enable, ~ready, buffer_status);  // AND_Gate
  Counter #(.max('h2), .width(2)) counter_1 (
    .clr(ack), .count(read_enable), .clk(clk), .Q(counter_1_q));  // open: load, up, D, carry
  and and_2 (and_2_out, ~counter_1_q[0], ~counter_1_q[1]);  // AND_Gate
  and and_3 (and_3_out, counter_1_q[0], ~counter_1_q[1]);  // AND_Gate
  and and_4 (and_4_out, ~counter_1_q[0], counter_1_q[1]);  // AND_Gate
  ROM #(.addrWidth(7), .dataWidth(4)) rom_1 (.addr(kb_input), .data(rom_1_data));
  Register #(.width(4)) register_1 (.D(rom_1_data), .en(and_2_out), .clk(clk), .Q(port_output[7:4]), .clr(ack));
  Register #(.width(4)) register_2 (.D(rom_1_data), .en(and_3_out), .clk(clk), .Q(port_output[3:0]), .clr(ack));
  D_Flip_Flop d_ff_1 (.D(and_4_out), .clk(and_4_out), .Q(ready), .reset(ack));  // open: Qn, preset

  // Notes on the sheet:
  //   contents of rom_1 (hex, n*v repeats v):
  //   49*0 1 2 3 4 5 6 7 8 9 39*0 a b c d e f
endmodule

module InputPort2 (
  input  ready,
  input  serial_in,
  output [7:0] status_byte
);

  Pull_Resistor pull_resistor_1 (.node(serial_in));

  assign status_byte = {serial_in, {6{1'b0}}, ready};
endmodule

module OutputPort3 (
  input  [7:0] bus_in,
  input  clk,
  input  out_3_enable,
  output [3:0] nibble0,
  output [3:0] nibble1
);

  Register register_1 (.D(bus_in), .en(out_3_enable), .clk(clk), .Q({nibble1, nibble0}));  // open: clr
endmodule

module OutputPort4 (
  input  [7:0] in_1,
  input  clk,
  input  out_4_write,
  input  ack_signal,
  output [7:0] out_bits,
  output acknowledge_flag
);

  wire and_1_out, d_ff_1_qn;

  and and_1 (and_1_out, clk, d_ff_1_qn);
  Register register_1 (.D(in_1), .en(out_4_write), .clk(clk), .Q(out_bits));  // open: clr
  D_Flip_Flop d_ff_1 (
    .D(out_4_write), .clk(and_1_out), .Q(acknowledge_flag), .Qn(d_ff_1_qn), .reset(ack_signal));  // open: preset
endmodule
